// Digital circuit P8D16A_2A main.dig as structural Verilog
module P8D16A_2A_main (
  input  CLK,
  input  D0,
  input  D1,
  input  D2,
  input  D3,
  input  D4,
  input  D5,
  input  D6,
  input  D7,
  input  INT,
  input  IRQ,
  output A0,
  output A1,
  output A2,
  output A3,
  output A4,
  output A5,
  output A6,
  output A7,
  output A8,
  output A9,
  output A10,
  output A11,
  output A12,
  output A13,
  output A14,
  output A15,
  output MR,
  output MW,
  output INTACK
);

  wire alu_1_f0, alu_1_fc, alu_1_fn, alu_1_fo, alu_1_o0, alu_1_o1, alu_1_o2, alu_1_o3, alu_1_o4, alu_1_o5,
       alu_1_o6, alu_1_o7, AO0, AO1, AO2, AO3, AO4, AO5, AO6, AO7, clock_1_clk, instruction_decoder_1_p27,
       instruction_decoder_1_p28, instruction_decoder_1_p29, instruction_decoder_1_p30,
       instruction_decoder_1_p31, instruction_decoder_1_p32, instruction_decoder_1_p33,
       instruction_decoder_1_p34, instruction_decoder_1_p35, instruction_decoder_1_p36,
       instruction_decoder_1_p37, instruction_decoder_1_p38, instruction_decoder_1_p39,
       instruction_decoder_1_p40, instruction_decoder_1_p41, instruction_decoder_1_p42,
       instruction_decoder_1_p43, mareg16_1_o0, mareg16_1_o1, mareg16_1_o2, mareg16_1_o3, mareg16_1_o4,
       mareg16_1_o5, mareg16_1_o6, mareg16_1_o7, mareg16_1_o8, mareg16_1_o9, mareg16_1_o10, mareg16_1_o11,
       mareg16_1_o12, mareg16_1_o13, mareg16_1_o14, mareg16_1_o15, pincontrol8b_2_o0, pincontrol8b_2_o1,
       pincontrol8b_2_o2, pincontrol8b_2_o3, pincontrol8b_2_o4, pincontrol8b_2_o5, pincontrol8b_2_o6,
       pincontrol8b_2_o7, T0, T1, T2, T3, T4, T5, T6, T7, undriven, undriven_2, undriven_3, undriven_4,
       undriven_5, undriven_6, undriven_7, undriven_8, undriven_9, undriven_10, undriven_11, undriven_12,
       undriven_13, undriven_14, undriven_15, undriven_16, undriven_17, undriven_18, undriven_19,
       undriven_20, undriven_21, undriven_22;

  PinControl8b pincontrol8b_1 (
    .E(MW), .D0(pincontrol8b_2_o0), .D1(pincontrol8b_2_o1), .D2(pincontrol8b_2_o2), .D3(pincontrol8b_2_o3),
    .D4(pincontrol8b_2_o4), .D5(pincontrol8b_2_o5), .D6(pincontrol8b_2_o6), .D7(pincontrol8b_2_o7), .O0(D0),
    .O1(D1), .O2(D2), .O3(D3), .O4(D4), .O5(D5), .O6(D6), .O7(D7));
  PinControl8b pincontrol8b_2 (
    .E(MR), .D0(D0), .D1(D1), .D2(D2), .D3(D3), .D4(D4), .D5(D5), .D6(D6), .D7(D7), .O0(pincontrol8b_2_o0),
    .O1(pincontrol8b_2_o1), .O2(pincontrol8b_2_o2), .O3(pincontrol8b_2_o3), .O4(pincontrol8b_2_o4),
    .O5(pincontrol8b_2_o5), .O6(pincontrol8b_2_o6), .O7(pincontrol8b_2_o7));
  ALU alu_1 (
    .E(1'b1), .A0(pincontrol8b_2_o0), .A1(pincontrol8b_2_o1), .A2(pincontrol8b_2_o2), .A3(pincontrol8b_2_o3),
    .A4(pincontrol8b_2_o4), .A5(pincontrol8b_2_o5), .A6(pincontrol8b_2_o6), .A7(pincontrol8b_2_o7), .B0(T0),
    .B1(T1), .B2(T2), .B3(T3), .B4(T4), .B5(T5), .B6(T6), .B7(T7), .B(instruction_decoder_1_p28),
    .C(instruction_decoder_1_p29), .ADD(instruction_decoder_1_p30), .AND(instruction_decoder_1_p31),
    .OR(instruction_decoder_1_p32), .NOT(instruction_decoder_1_p33), .XOR(instruction_decoder_1_p34),
    .SL(instruction_decoder_1_p35), .SR(instruction_decoder_1_p36), .RL(instruction_decoder_1_p37),
    .RR(instruction_decoder_1_p38), .O0(alu_1_o0), .O1(alu_1_o1), .O2(alu_1_o2), .O3(alu_1_o3),
    .O4(alu_1_o4), .O5(alu_1_o5), .O6(alu_1_o6), .O7(alu_1_o7), .F0(alu_1_f0), .FC(alu_1_fc), .FO(alu_1_fo),
    .FN(alu_1_fn));
  Register register_1 (
    .CLK(clock_1_clk), .E(1'b1), .R(undriven_15), .W(instruction_decoder_1_p27), .D0(alu_1_o0),
    .D1(alu_1_o1), .D2(alu_1_o2), .D3(alu_1_o3), .D4(alu_1_o4), .D5(alu_1_o5), .D6(alu_1_o6), .D7(alu_1_o7),
    .O0(pincontrol8b_2_o0), .O1(pincontrol8b_2_o1), .O2(pincontrol8b_2_o2), .O3(pincontrol8b_2_o3),
    .O4(pincontrol8b_2_o4), .O5(pincontrol8b_2_o5), .O6(pincontrol8b_2_o6), .O7(pincontrol8b_2_o7));
  Register A (
    .CLK(clock_1_clk), .E(1'b1), .R(1'b1), .W(instruction_decoder_1_p40), .D0(pincontrol8b_2_o0),
    .D1(pincontrol8b_2_o1), .D2(pincontrol8b_2_o2), .D3(pincontrol8b_2_o3), .D4(pincontrol8b_2_o4),
    .D5(pincontrol8b_2_o5), .D6(pincontrol8b_2_o6), .D7(pincontrol8b_2_o7), .O0(AO0), .O1(AO1), .O2(AO2),
    .O3(AO3), .O4(AO4), .O5(AO5), .O6(AO6), .O7(AO7));
  PinControl8b pincontrol8b_3 (
    .E(instruction_decoder_1_p39), .D0(AO0), .D1(AO1), .D2(AO2), .D3(AO3), .D4(AO4), .D5(AO5), .D6(AO6),
    .D7(AO7), .O0(pincontrol8b_2_o0), .O1(pincontrol8b_2_o1), .O2(pincontrol8b_2_o2), .O3(pincontrol8b_2_o3),
    .O4(pincontrol8b_2_o4), .O5(pincontrol8b_2_o5), .O6(pincontrol8b_2_o6), .O7(pincontrol8b_2_o7));
  Register X (
    .CLK(clock_1_clk), .E(1'b1), .R(instruction_decoder_1_p42), .W(instruction_decoder_1_p41),
    .D0(pincontrol8b_2_o0), .D1(pincontrol8b_2_o1), .D2(pincontrol8b_2_o2), .D3(pincontrol8b_2_o3),
    .D4(pincontrol8b_2_o4), .D5(pincontrol8b_2_o5), .D6(pincontrol8b_2_o6), .D7(pincontrol8b_2_o7),
    .O0(pincontrol8b_2_o0), .O1(pincontrol8b_2_o1), .O2(pincontrol8b_2_o2), .O3(pincontrol8b_2_o3),
    .O4(pincontrol8b_2_o4), .O5(pincontrol8b_2_o5), .O6(pincontrol8b_2_o6), .O7(pincontrol8b_2_o7));
  StackPointer SP (
    .CLK(clock_1_clk), .INC(undriven_18), .DEC(undriven_19), .R(undriven_21), .W(undriven_22),
    .D0(pincontrol8b_2_o0), .D1(pincontrol8b_2_o1), .D2(pincontrol8b_2_o2), .D3(pincontrol8b_2_o3),
    .D4(pincontrol8b_2_o4), .D5(pincontrol8b_2_o5), .D6(pincontrol8b_2_o6), .D7(pincontrol8b_2_o7),
    .O0(pincontrol8b_2_o0), .O1(pincontrol8b_2_o1), .O2(pincontrol8b_2_o2), .O3(pincontrol8b_2_o3),
    .O4(pincontrol8b_2_o4), .O5(pincontrol8b_2_o5), .O6(pincontrol8b_2_o6), .O7(pincontrol8b_2_o7));
  Register Y (
    .CLK(clock_1_clk), .E(1'b1), .R(instruction_decoder_1_p43), .W(undriven_20), .D0(pincontrol8b_2_o0),
    .D1(pincontrol8b_2_o1), .D2(pincontrol8b_2_o2), .D3(pincontrol8b_2_o3), .D4(pincontrol8b_2_o4),
    .D5(pincontrol8b_2_o5), .D6(pincontrol8b_2_o6), .D7(pincontrol8b_2_o7), .O0(pincontrol8b_2_o0),
    .O1(pincontrol8b_2_o1), .O2(pincontrol8b_2_o2), .O3(pincontrol8b_2_o3), .O4(pincontrol8b_2_o4),
    .O5(pincontrol8b_2_o5), .O6(pincontrol8b_2_o6), .O7(pincontrol8b_2_o7));
  Clock clock_1 (.HLT(undriven_17), .Clock(CLK), .M_CLK(1'b0), .M_E(1'b0), .CLK(clock_1_clk));
  Reg16 L (
    .CLK(clock_1_clk), .E(1'b1), .R(undriven_5), .W(undriven_4), .D0(undriven_3), .D1(undriven),
    .D2(pincontrol8b_2_o0), .D3(pincontrol8b_2_o1), .D4(pincontrol8b_2_o2), .D5(pincontrol8b_2_o3),
    .D6(pincontrol8b_2_o4), .D7(pincontrol8b_2_o5), .D8(pincontrol8b_2_o6), .D9(pincontrol8b_2_o7),
    .O0(pincontrol8b_2_o0), .O1(pincontrol8b_2_o1), .O2(pincontrol8b_2_o2), .O3(pincontrol8b_2_o3),
    .O4(pincontrol8b_2_o4), .O5(pincontrol8b_2_o5), .O6(pincontrol8b_2_o6), .O7(pincontrol8b_2_o7));  // open: D10, D11, D12, D13, D14, D15, O8, O9, O10, O11, O12, O13, O14, O15
  Register Z (
    .CLK(clock_1_clk), .E(1'b1), .R(undriven_14), .W(undriven_2), .D0(pincontrol8b_2_o0),
    .D1(pincontrol8b_2_o1), .D2(pincontrol8b_2_o2), .D3(pincontrol8b_2_o3), .D4(pincontrol8b_2_o4),
    .D5(pincontrol8b_2_o5), .D6(pincontrol8b_2_o6), .D7(pincontrol8b_2_o7), .O0(pincontrol8b_2_o0),
    .O1(pincontrol8b_2_o1), .O2(pincontrol8b_2_o2), .O3(pincontrol8b_2_o3), .O4(pincontrol8b_2_o4),
    .O5(pincontrol8b_2_o5), .O6(pincontrol8b_2_o6), .O7(pincontrol8b_2_o7));
  ProgramCounter16 PC (
    .CLK(clock_1_clk), .E(undriven_10), .RL(undriven_9), .WL(undriven_8), .RH(undriven_7), .WH(undriven_6),
    .D0(pincontrol8b_2_o0), .D1(pincontrol8b_2_o1), .D2(pincontrol8b_2_o2), .D3(pincontrol8b_2_o3),
    .D4(pincontrol8b_2_o4), .D5(pincontrol8b_2_o5), .D6(pincontrol8b_2_o6), .D7(pincontrol8b_2_o7),
    .O0(pincontrol8b_2_o0), .O1(pincontrol8b_2_o1), .O2(pincontrol8b_2_o2), .O3(pincontrol8b_2_o3),
    .O4(pincontrol8b_2_o4), .O5(pincontrol8b_2_o5), .O6(pincontrol8b_2_o6), .O7(pincontrol8b_2_o7));
  Register T (
    .CLK(clock_1_clk), .E(1'b1), .R(1'b1), .W(undriven_16), .D0(pincontrol8b_2_o0), .D1(pincontrol8b_2_o1),
    .D2(pincontrol8b_2_o2), .D3(pincontrol8b_2_o3), .D4(pincontrol8b_2_o4), .D5(pincontrol8b_2_o5),
    .D6(pincontrol8b_2_o6), .D7(pincontrol8b_2_o7), .O0(T0), .O1(T1), .O2(T2), .O3(T3), .O4(T4), .O5(T5),
    .O6(T6), .O7(T7));
  MAReg16 mareg16_1 (
    .CLK(clock_1_clk), .INC(undriven_13), .DEC(1'b0), .WL(undriven_12), .WH(undriven_11),
    .D0(pincontrol8b_2_o0), .D1(pincontrol8b_2_o1), .D2(pincontrol8b_2_o2), .D3(pincontrol8b_2_o3),
    .D4(pincontrol8b_2_o4), .D5(pincontrol8b_2_o5), .D6(pincontrol8b_2_o6), .D7(pincontrol8b_2_o7),
    .O0(mareg16_1_o0), .O1(mareg16_1_o1), .O2(mareg16_1_o2), .O3(mareg16_1_o3), .O4(mareg16_1_o4),
    .O5(mareg16_1_o5), .O6(mareg16_1_o6), .O7(mareg16_1_o7), .O8(mareg16_1_o8), .O9(mareg16_1_o9),
    .O10(mareg16_1_o10), .O11(mareg16_1_o11), .O12(mareg16_1_o12), .O13(mareg16_1_o13), .O14(mareg16_1_o14),
    .O15(mareg16_1_o15));
  // Instruction_Decoder instruction_decoder_1: pin names not known; wires that end beside it: T1, T2, T3, clock_1_clk, pincontrol8b_2_o0, pincontrol8b_2_o1, pincontrol8b_2_o2, pincontrol8b_2_o3, pincontrol8b_2_o4, pincontrol8b_2_o5, pincontrol8b_2_o6, pincontrol8b_2_o7, IRQ, INT, alu_1_f0, alu_1_fc, alu_1_fo, alu_1_fn, pincontrol8b_2_o0, pincontrol8b_2_o1, pincontrol8b_2_o2, pincontrol8b_2_o3, pincontrol8b_2_o4, pincontrol8b_2_o5, pincontrol8b_2_o6, pincontrol8b_2_o7, instruction_decoder_1_p27, instruction_decoder_1_p28, instruction_decoder_1_p29, instruction_decoder_1_p30, instruction_decoder_1_p31, instruction_decoder_1_p32, instruction_decoder_1_p33, instruction_decoder_1_p34, instruction_decoder_1_p35, instruction_decoder_1_p36, instruction_decoder_1_p37, instruction_decoder_1_p38, instruction_decoder_1_p39, instruction_decoder_1_p40, instruction_decoder_1_p41, instruction_decoder_1_p42, instruction_decoder_1_p43
  PinControl8b pincontrol8b_4 (
    .E(1'b1), .D0(mareg16_1_o0), .D1(mareg16_1_o1), .D2(mareg16_1_o2), .D3(mareg16_1_o3), .D4(mareg16_1_o4),
    .D5(mareg16_1_o5), .D6(mareg16_1_o6), .D7(mareg16_1_o7), .O0(A0), .O1(A1), .O2(A2), .O3(A3), .O4(A4),
    .O5(A5), .O6(A6), .O7(A7));
  PinControl8b pincontrol8b_5 (
    .E(1'b1), .D0(mareg16_1_o8), .D1(mareg16_1_o9), .D2(mareg16_1_o10), .D3(mareg16_1_o11),
    .D4(mareg16_1_o12), .D5(mareg16_1_o13), .D6(mareg16_1_o14), .D7(mareg16_1_o15), .O0(A8), .O1(A9),
    .O2(A10), .O3(A11), .O4(A12), .O5(A13), .O6(A14), .O7(A15));

  // Notes on the sheet:
  //   DB OUT
  //   DB IN
  //   A W/R/  /CLK
  //   X W/R/CLK
  //   SP W/R/--/++/CLK
  //   Y W/R/CLK
  //   L WH/RH/WL/RL/CLK
  //   Z W/R/CLK
  //   PC WH/RH/WL/RL/E/CLK
  //   TW
  //   MA WH/WL/INC/CLK
  //   INT/IRQ/CLK
  //   Address Bus
  //   AB OUT
endmodule
