// Digital circuit P8D16A_2A_Assembly.dig as structural Verilog
module P8D16A_2A_Assembly (
  input  CLK
);

  wire button_1_out, button_2_out, p8d16a_2a_main_1_a0, p8d16a_2a_main_1_a1, p8d16a_2a_main_1_a2,
       p8d16a_2a_main_1_a3, p8d16a_2a_main_1_a4, p8d16a_2a_main_1_a5, p8d16a_2a_main_1_a6,
       p8d16a_2a_main_1_a7, p8d16a_2a_main_1_a8, p8d16a_2a_main_1_a9, p8d16a_2a_main_1_a10,
       p8d16a_2a_main_1_a11, p8d16a_2a_main_1_a12, p8d16a_2a_main_1_a13, p8d16a_2a_main_1_a14,
       p8d16a_2a_main_1_a15, p8d16a_2a_main_1_intack, p8d16a_2a_main_1_mr, p8d16a_2a_main_1_mw;
  wire [3:0] fumemory16_1_o3, fumemory16_1_o7;

  Button button_1 (.out(button_1_out));
  Button button_2 (.out(button_2_out));
  P8D16A_2A_main p8d16a_2a_main_1 (
    .CLK(CLK), .D0(fumemory16_1_o3[3]), .D1(fumemory16_1_o3[2]), .D2(fumemory16_1_o3[1]),
    .D3(fumemory16_1_o3[0]), .D4(fumemory16_1_o7[3]), .D5(fumemory16_1_o7[2]), .D6(fumemory16_1_o7[1]),
    .D7(fumemory16_1_o7[0]), .INT(button_1_out), .IRQ(button_2_out), .A0(p8d16a_2a_main_1_a0),
    .A1(p8d16a_2a_main_1_a1), .A2(p8d16a_2a_main_1_a2), .A3(p8d16a_2a_main_1_a3), .A4(p8d16a_2a_main_1_a4),
    .A5(p8d16a_2a_main_1_a5), .A6(p8d16a_2a_main_1_a6), .A7(p8d16a_2a_main_1_a7), .A8(p8d16a_2a_main_1_a8),
    .A9(p8d16a_2a_main_1_a9), .A10(p8d16a_2a_main_1_a10), .A11(p8d16a_2a_main_1_a11),
    .A12(p8d16a_2a_main_1_a12), .A13(p8d16a_2a_main_1_a13), .A14(p8d16a_2a_main_1_a14),
    .A15(p8d16a_2a_main_1_a15), .MR(p8d16a_2a_main_1_mr), .MW(p8d16a_2a_main_1_mw),
    .INTACK(p8d16a_2a_main_1_intack));
  LED led_1 (.in(p8d16a_2a_main_1_intack));
  FUMemory16 fumemory16_1 (
    .CLK(CLK), .R(p8d16a_2a_main_1_mr), .W(p8d16a_2a_main_1_mw), .E(1'b1), .A0(p8d16a_2a_main_1_a0),
    .A1(p8d16a_2a_main_1_a1), .A2(p8d16a_2a_main_1_a2), .A3(p8d16a_2a_main_1_a3), .A4(p8d16a_2a_main_1_a4),
    .A5(p8d16a_2a_main_1_a5), .A6(p8d16a_2a_main_1_a6), .A7(p8d16a_2a_main_1_a7), .A8(p8d16a_2a_main_1_a8),
    .A9(p8d16a_2a_main_1_a9), .A10(p8d16a_2a_main_1_a10), .A11(p8d16a_2a_main_1_a11),
    .A12(p8d16a_2a_main_1_a12), .A13(p8d16a_2a_main_1_a13), .A14(p8d16a_2a_main_1_a14),
    .A15(p8d16a_2a_main_1_a15), .D0(fumemory16_1_o3[3]), .D1(fumemory16_1_o3[2]), .D2(fumemory16_1_o3[1]),
    .D3(fumemory16_1_o3[0]), .D4(fumemory16_1_o7[3]), .D5(fumemory16_1_o7[2]), .D6(fumemory16_1_o7[1]),
    .D7(fumemory16_1_o7[0]), .O0(fumemory16_1_o3[3]), .O1(fumemory16_1_o3[2]), .O2(fumemory16_1_o3[1]),
    .O3(fumemory16_1_o3[0]), .O4(fumemory16_1_o7[3]), .O5(fumemory16_1_o7[2]), .O6(fumemory16_1_o7[1]),
    .O7(fumemory16_1_o7[0]));
  Seven_Seg_Hex seven_seg_hex_1 (.d(fumemory16_1_o3), .dp(1'b0));
  Seven_Seg_Hex seven_seg_hex_2 (.d(fumemory16_1_o7), .dp(1'b0));

  // Notes on the sheet:
  //   CLK: Hz: 5
endmodule
