// Digital circuit P8D16A_2A_InternalAssembly.dig as structural Verilog
module P8D16A_2A_InternalAssembly (
  input  CLK,
  input  INT,
  input  IRQ,
  output INTACK
);

  wire A0, A1, A2, A3, A4, A5, A6, A7, A8, A9, A10, A11, A12, A13, A14, A15, alu_1_f0, alu_1_fc, alu_1_fn,
       alu_1_fo, alu_1_o0, alu_1_o1, alu_1_o2, alu_1_o3, alu_1_o4, alu_1_o5, alu_1_o6, alu_1_o7, and_1_out,
       AO0, AO1, AO2, AO3, AO4, AO5, AO6, AO7, B0, B1, B2, B3, B4, B5, B6, B7, BI0, BI1, BI2, BI3, BI4, BI5,
       BI6, BI7, CLK_t, delay_1_out, dipswitch_1_out, dipswitch_2_out, I0, I1, I2, I3, I4, I5, I6, I7,
       instruction_decoder_1_alu_b, instruction_decoder_1_aluadd, instruction_decoder_1_aluand,
       instruction_decoder_1_aluc, instruction_decoder_1_alue, instruction_decoder_1_alunot,
       instruction_decoder_1_aluor, instruction_decoder_1_alurl, instruction_decoder_1_alurr,
       instruction_decoder_1_alusl, instruction_decoder_1_alusr, instruction_decoder_1_aluxor,
       instruction_decoder_1_ar, instruction_decoder_1_aw, instruction_decoder_1_hlt,
       instruction_decoder_1_lhr, instruction_decoder_1_lhw, instruction_decoder_1_llr,
       instruction_decoder_1_llw, instruction_decoder_1_madec, instruction_decoder_1_mahw,
       instruction_decoder_1_mainc, instruction_decoder_1_malw, instruction_decoder_1_pce,
       instruction_decoder_1_pchr, instruction_decoder_1_pchw, instruction_decoder_1_pclr,
       instruction_decoder_1_pclw, instruction_decoder_1_spdec, instruction_decoder_1_spinc,
       instruction_decoder_1_spr, instruction_decoder_1_spw, instruction_decoder_1_trr,
       instruction_decoder_1_tw, instruction_decoder_1_xr, instruction_decoder_1_xw,
       instruction_decoder_1_yr, instruction_decoder_1_yw, instruction_decoder_1_zr,
       instruction_decoder_1_zw, mareg16_1_o0, mareg16_1_o1, mareg16_1_o2, mareg16_1_o3, mareg16_1_o4,
       mareg16_1_o5, mareg16_1_o6, mareg16_1_o7, mareg16_1_o8, mareg16_1_o9, mareg16_1_o10, mareg16_1_o11,
       mareg16_1_o12, mareg16_1_o13, mareg16_1_o14, mareg16_1_o15, MR, MW, rising_edge_detector_1_out, T0,
       T1, T2, T3, T4, T5, T6, T7, Z0, Z1, Z2, Z3, Z4, Z5, Z6, Z7;
  wire [7:0] d_ff_1_q;

  PinControl8b pincontrol8b_1 (
    .E(MW), .D0(BI0), .D1(BI1), .D2(BI2), .D3(BI3), .D4(BI4), .D5(BI5), .D6(BI6), .D7(BI7), .O0(B0), .O1(B1),
    .O2(B2), .O3(B3), .O4(B4), .O5(B5), .O6(B6), .O7(B7));
  PinControl8b pincontrol8b_2 (
    .E(MR), .D0(B0), .D1(B1), .D2(B2), .D3(B3), .D4(B4), .D5(B5), .D6(B6), .D7(B7), .O0(BI0), .O1(BI1),
    .O2(BI2), .O3(BI3), .O4(BI4), .O5(BI5), .O6(BI6), .O7(BI7));
  ALU alu_1 (
    .E(1'b1), .A0(BI0), .A1(BI1), .A2(BI2), .A3(BI3), .A4(BI4), .A5(BI5), .A6(BI6), .A7(BI7), .B0(T0),
    .B1(T1), .B2(T2), .B3(T3), .B4(T4), .B5(T5), .B6(T6), .B7(T7), .B(instruction_decoder_1_alu_b),
    .C(instruction_decoder_1_aluc), .ADD(instruction_decoder_1_aluadd), .AND(instruction_decoder_1_aluand),
    .OR(instruction_decoder_1_aluor), .NOT(instruction_decoder_1_alunot), .XOR(instruction_decoder_1_aluxor),
    .SL(instruction_decoder_1_alusl), .SR(instruction_decoder_1_alusr), .RL(instruction_decoder_1_alurl),
    .RR(instruction_decoder_1_alurr), .O0(alu_1_o0), .O1(alu_1_o1), .O2(alu_1_o2), .O3(alu_1_o3),
    .O4(alu_1_o4), .O5(alu_1_o5), .O6(alu_1_o6), .O7(alu_1_o7), .F0(alu_1_f0), .FC(alu_1_fc), .FO(alu_1_fo),
    .FN(alu_1_fn));
  Register register_1 (
    .CLK(CLK_t), .E(1'b1), .R(instruction_decoder_1_trr), .W(instruction_decoder_1_alue), .D0(alu_1_o0),
    .D1(alu_1_o1), .D2(alu_1_o2), .D3(alu_1_o3), .D4(alu_1_o4), .D5(alu_1_o5), .D6(alu_1_o6), .D7(alu_1_o7),
    .O0(BI0), .O1(BI1), .O2(BI2), .O3(BI3), .O4(BI4), .O5(BI5), .O6(BI6), .O7(BI7));
  Register A (
    .CLK(CLK_t), .E(1'b1), .R(1'b1), .W(instruction_decoder_1_aw), .D0(BI0), .D1(BI1), .D2(BI2), .D3(BI3),
    .D4(BI4), .D5(BI5), .D6(BI6), .D7(BI7), .O0(AO0), .O1(AO1), .O2(AO2), .O3(AO3), .O4(AO4), .O5(AO5),
    .O6(AO6), .O7(AO7));
  PinControl8b pincontrol8b_3 (
    .E(instruction_decoder_1_ar), .D0(AO0), .D1(AO1), .D2(AO2), .D3(AO3), .D4(AO4), .D5(AO5), .D6(AO6),
    .D7(AO7), .O0(BI0), .O1(BI1), .O2(BI2), .O3(BI3), .O4(BI4), .O5(BI5), .O6(BI6), .O7(BI7));
  Register X (
    .CLK(CLK_t), .E(1'b1), .R(instruction_decoder_1_xw), .W(instruction_decoder_1_xr), .D0(BI0), .D1(BI1),
    .D2(BI2), .D3(BI3), .D4(BI4), .D5(BI5), .D6(BI6), .D7(BI7), .O0(BI0), .O1(BI1), .O2(BI2), .O3(BI3),
    .O4(BI4), .O5(BI5), .O6(BI6), .O7(BI7));
  StackPointer SP (
    .CLK(CLK_t), .INC(instruction_decoder_1_spinc), .DEC(instruction_decoder_1_spdec),
    .R(instruction_decoder_1_spr), .W(instruction_decoder_1_spw), .D0(BI0), .D1(BI1), .D2(BI2), .D3(BI3),
    .D4(BI4), .D5(BI5), .D6(BI6), .D7(BI7), .O0(BI0), .O1(BI1), .O2(BI2), .O3(BI3), .O4(BI4), .O5(BI5),
    .O6(BI6), .O7(BI7));
  Register Y (
    .CLK(CLK_t), .E(1'b1), .R(instruction_decoder_1_yr), .W(instruction_decoder_1_yw), .D0(BI0), .D1(BI1),
    .D2(BI2), .D3(BI3), .D4(BI4), .D5(BI5), .D6(BI6), .D7(BI7), .O0(BI0), .O1(BI1), .O2(BI2), .O3(BI3),
    .O4(BI4), .O5(BI5), .O6(BI6), .O7(BI7));
  Register Z (
    .CLK(delay_1_out), .E(1'b1), .R(1'b1), .W(instruction_decoder_1_zw), .D0(BI0), .D1(BI1), .D2(BI2),
    .D3(BI3), .D4(BI4), .D5(BI5), .D6(BI6), .D7(BI7), .O0(Z0), .O1(Z1), .O2(Z2), .O3(Z3), .O4(Z4), .O5(Z5),
    .O6(Z6), .O7(Z7));
  Delay #(.delayTime(20)) delay_1 (.in(CLK_t), .out(delay_1_out));
  Reg16 L (
    .CLK(CLK_t), .E(1'b1), .R(instruction_decoder_1_llr), .W(instruction_decoder_1_llw),
    .D0(instruction_decoder_1_lhr), .D1(instruction_decoder_1_lhw), .D2(BI0), .D3(BI1), .D4(BI2), .D5(BI3),
    .D6(BI4), .D7(BI5), .D8(BI6), .D9(BI7), .O0(BI0), .O1(BI1), .O2(BI2), .O3(BI3), .O4(BI4), .O5(BI5),
    .O6(BI6), .O7(BI7));  // open: D10, D11, D12, D13, D14, D15, O8, O9, O10, O11, O12, O13, O14, O15
  DipSwitch #(.dipDefault("true")) dipswitch_1 (.out(dipswitch_1_out));
  PinControl8b pincontrol8b_4 (
    .E(instruction_decoder_1_zr), .D0(Z0), .D1(Z1), .D2(Z2), .D3(Z3), .D4(Z4), .D5(Z5), .D6(Z6), .D7(Z7),
    .O0(BI0), .O1(BI1), .O2(BI2), .O3(BI3), .O4(BI4), .O5(BI5), .O6(BI6), .O7(BI7));
  Clock clock_1 (
    .HLT(instruction_decoder_1_hlt), .Clock(CLK), .M_CLK(dipswitch_1_out), .M_E(dipswitch_2_out), .CLK(CLK_t));
  DipSwitch #(.dipDefault("true")) dipswitch_2 (.out(dipswitch_2_out));
  ProgramCounter16 PC (
    .CLK(CLK_t), .E(instruction_decoder_1_pce), .RL(instruction_decoder_1_pclr),
    .WL(instruction_decoder_1_pclw), .RH(instruction_decoder_1_pchr), .WH(instruction_decoder_1_pchw),
    .D0(BI0), .D1(BI1), .D2(BI2), .D3(BI3), .D4(BI4), .D5(BI5), .D6(BI6), .D7(BI7), .O0(BI0), .O1(BI1),
    .O2(BI2), .O3(BI3), .O4(BI4), .O5(BI5), .O6(BI6), .O7(BI7));
  Register T (
    .CLK(CLK_t), .E(1'b1), .R(1'b1), .W(instruction_decoder_1_tw), .D0(BI0), .D1(BI1), .D2(BI2), .D3(BI3),
    .D4(BI4), .D5(BI5), .D6(BI6), .D7(BI7), .O0(T0), .O1(T1), .O2(T2), .O3(T3), .O4(T4), .O5(T5), .O6(T6),
    .O7(T7));
  MAReg16 mareg16_1 (
    .CLK(CLK_t), .INC(instruction_decoder_1_mainc), .DEC(instruction_decoder_1_madec),
    .WL(instruction_decoder_1_malw), .WH(instruction_decoder_1_mahw), .D0(BI0), .D1(BI1), .D2(BI2), .D3(BI3),
    .D4(BI4), .D5(BI5), .D6(BI6), .D7(BI7), .O0(mareg16_1_o0), .O1(mareg16_1_o1), .O2(mareg16_1_o2),
    .O3(mareg16_1_o3), .O4(mareg16_1_o4), .O5(mareg16_1_o5), .O6(mareg16_1_o6), .O7(mareg16_1_o7),
    .O8(mareg16_1_o8), .O9(mareg16_1_o9), .O10(mareg16_1_o10), .O11(mareg16_1_o11), .O12(mareg16_1_o12),
    .O13(mareg16_1_o13), .O14(mareg16_1_o14), .O15(mareg16_1_o15));
  Instruction_Decoder instruction_decoder_1 (
    .CLK(CLK_t), .I0(BI0), .I1(BI1), .I2(BI2), .I3(BI3), .I4(BI4), .I5(BI5), .I6(BI6), .I7(BI7), .IRQ(IRQ),
    .INT(INT), .F0(alu_1_f0), .FC(alu_1_fc), .FO(alu_1_fo), .FN(alu_1_fn), .D0(BI0), .D1(BI1), .D2(BI2),
    .D3(BI3), .D4(BI4), .D5(BI5), .D6(BI6), .D7(BI7), .ALUE(instruction_decoder_1_alue),
    .ALU_B(instruction_decoder_1_alu_b), .ALUC(instruction_decoder_1_aluc),
    .ALUADD(instruction_decoder_1_aluadd), .ALUAND(instruction_decoder_1_aluand),
    .ALUOR(instruction_decoder_1_aluor), .ALUNOT(instruction_decoder_1_alunot),
    .ALUXOR(instruction_decoder_1_aluxor), .ALUSL(instruction_decoder_1_alusl),
    .ALUSR(instruction_decoder_1_alusr), .ALURL(instruction_decoder_1_alurl),
    .ALURR(instruction_decoder_1_alurr), .AR(instruction_decoder_1_ar), .AW(instruction_decoder_1_aw),
    .XR(instruction_decoder_1_xr), .XW(instruction_decoder_1_xw), .YR(instruction_decoder_1_yr),
    .YW(instruction_decoder_1_yw), .ZR(instruction_decoder_1_zr), .ZW(instruction_decoder_1_zw),
    .PCE(instruction_decoder_1_pce), .PCHR(instruction_decoder_1_pchr), .PCHW(instruction_decoder_1_pchw),
    .PCLR(instruction_decoder_1_pclr), .PCLW(instruction_decoder_1_pclw), .SPR(instruction_decoder_1_spr),
    .SPW(instruction_decoder_1_spw), .SPINC(instruction_decoder_1_spinc),
    .SPDEC(instruction_decoder_1_spdec), .LHR(instruction_decoder_1_lhr), .LHW(instruction_decoder_1_lhw),
    .LLR(instruction_decoder_1_llr), .LLW(instruction_decoder_1_llw), .MALW(instruction_decoder_1_malw),
    .MAHW(instruction_decoder_1_mahw), .INTACK(INTACK), .HLT(instruction_decoder_1_hlt),
    .TRR(instruction_decoder_1_trr), .MR(MR), .MW(MW), .TW(instruction_decoder_1_tw),
    .MAINC(instruction_decoder_1_mainc), .MADEC(instruction_decoder_1_madec), .I_0(I0), .I_1(I1), .I_2(I2),
    .I_3(I3), .I_4(I4), .I_5(I5), .I_6(I6), .I_7(I7));
  PinControl8b pincontrol8b_5 (
    .E(1'b1), .D0(mareg16_1_o0), .D1(mareg16_1_o1), .D2(mareg16_1_o2), .D3(mareg16_1_o3), .D4(mareg16_1_o4),
    .D5(mareg16_1_o5), .D6(mareg16_1_o6), .D7(mareg16_1_o7), .O0(A0), .O1(A1), .O2(A2), .O3(A3), .O4(A4),
    .O5(A5), .O6(A6), .O7(A7));
  PinControl8b pincontrol8b_6 (
    .E(1'b1), .D0(mareg16_1_o8), .D1(mareg16_1_o9), .D2(mareg16_1_o10), .D3(mareg16_1_o11),
    .D4(mareg16_1_o12), .D5(mareg16_1_o13), .D6(mareg16_1_o14), .D7(mareg16_1_o15), .O0(A8), .O1(A9),
    .O2(A10), .O3(A11), .O4(A12), .O5(A13), .O6(A14), .O7(A15));
  Rising_Edge_Detector rising_edge_detector_1 (.CLK(CLK_t), .OUT(rising_edge_detector_1_out));
  and and_1 (and_1_out, rising_edge_detector_1_out, MR);
  FUMemory16 fumemory16_1 (
    .CLK(CLK_t), .R(MR), .W(MW), .E(1'b1), .A0(A0), .A1(A1), .A2(A2), .A3(A3), .A4(A4), .A5(A5), .A6(A6),
    .A7(A7), .A8(A8), .A9(A9), .A10(A10), .A11(A11), .A12(A12), .A13(A13), .A14(A14), .A15(A15), .D0(B0),
    .D1(B1), .D2(B2), .D3(B3), .D4(B4), .D5(B5), .D6(B6), .D7(B7), .O0(B0), .O1(B1), .O2(B2), .O3(B3),
    .O4(B4), .O5(B5), .O6(B6), .O7(B7));
  Seven_Seg_Hex seven_seg_hex_1 (.d({I0, I1, I2, I3}), .dp(1'b0));
  Seven_Seg_Hex seven_seg_hex_2 (.d({I4, I5, I6, I7}), .dp(1'b0));
  Seven_Seg_Hex seven_seg_hex_3 (.d({A0, A1, A2, A3}), .dp(1'b0));
  D_FF #(.Bits(8)) d_ff_1 (.D({B0, B1, B2, B3, B4, B5, B6, B7}), .C(and_1_out), .Q(d_ff_1_q));  // open: nQ
  Seven_Seg_Hex seven_seg_hex_4 (.d({A4, A5, A6, A7}), .dp(1'b0));
  Seven_Seg_Hex seven_seg_hex_5 (.d({BI0, BI1, BI2, BI3}), .dp(1'b0));
  Seven_Seg_Hex seven_seg_hex_6 (.d({Z0, Z1, Z2, Z3}), .dp(1'b0));
  Seven_Seg_Hex seven_seg_hex_7 (.d({AO0, AO1, AO2, AO3}), .dp(1'b0));
  // Probe on d_ff_1_q
  Seven_Seg_Hex seven_seg_hex_8 (.d({B0, B1, B2, B3}), .dp(1'b0));
  Seven_Seg_Hex seven_seg_hex_9 (.d({A8, A9, A10, A11}), .dp(1'b0));
  Seven_Seg_Hex seven_seg_hex_10 (.d({BI4, BI5, BI6, BI7}), .dp(1'b0));
  Seven_Seg_Hex seven_seg_hex_11 (.d({Z4, Z5, Z6, Z7}), .dp(1'b0));
  Seven_Seg_Hex seven_seg_hex_12 (.d({AO4, AO5, AO6, AO7}), .dp(1'b0));
  Seven_Seg_Hex seven_seg_hex_13 (.d({A12, A13, A14, A15}), .dp(1'b0));
  Seven_Seg_Hex seven_seg_hex_14 (.d({B4, B5, B6, B7}), .dp(1'b0));

  // Notes on the sheet:
  //   CLK: Hz: 5
  //   DB OUT
  //   DB IN
  //   A W/R/  /CLK
  //   X W/R/CLK
  //   SP W/R/--/++/CLK
  //   Y W/R/CLK
  //   L WH/RH/WL/RL/CLK
  //   Z W/R/CLK
  //   PC WH/RH/WL/RL/E/CLK
  //   TW
  //   MA WH/WL/INC/CLK
  //   INT/IRQ/CLK
  //   Address Bus
  //   AB OUT
  //   I REGISTER
  //   ADDRESS BUS
  //   I DATA BUS
  //   Z REGISTER
  //   A REGISTER
  //   E DATA BUS
endmodule
