// Digital circuit AddressDecoder16b.dig as structural Verilog
module AddressDecoder16b (
  input  A0,
  input  A1,
  input  A2,
  input  A3,
  input  A4,
  input  A5,
  input  A6,
  input  A7,
  input  A8,
  input  A9,
  input  A10,
  input  A11,
  input  A12,
  input  A13,
  input  A14,
  input  A15,
  output I_O,
  output MEM
);

  wire and_1_out, not_1_out, not_2_out, not_3_out, not_4_out, or_1_out;

  and and_1 (and_1_out, A0, A1, A2, A3, A4, A5, A6, A7);
  not not_1 (not_1_out, A8);
  not not_2 (not_2_out, A9);
  not not_3 (not_3_out, A10);
  not not_4 (not_4_out, A11);
  or or_1 (or_1_out, not_1_out, not_2_out, not_3_out, not_4_out);
  and and_2 (I_O, and_1_out, or_1_out);
  not not_5 (MEM, I_O);
endmodule
