// Digital circuit And8b.dig as structural Verilog
module And8b (
  input  E,
  input  X0,
  input  X1,
  input  X2,
  input  X3,
  input  X4,
  input  X5,
  input  X6,
  input  X7,
  input  Y0,
  input  Y1,
  input  Y2,
  input  Y3,
  input  Y4,
  input  Y5,
  input  Y6,
  input  Y7,
  output O0,
  output O1,
  output O2,
  output O3,
  output O4,
  output O5,
  output O6,
  output O7
);

  wire and_1_out, and_2_out, and_3_out, and_4_out, and_5_out, and_6_out, and_7_out, and_8_out;

  and and_1 (and_1_out, X7, Y7);
  and and_2 (and_2_out, X6, Y6);
  and and_3 (and_3_out, X5, Y5);
  and and_4 (and_4_out, X4, Y4);
  and and_5 (and_5_out, X3, Y3);
  and and_6 (and_6_out, X2, Y2);
  and and_7 (and_7_out, X1, Y1);
  and and_8 (and_8_out, X0, Y0);
  PinControl8b pincontrol8b_1 (
    .E(E), .D0(and_8_out), .D1(and_7_out), .D2(and_6_out), .D3(and_5_out), .D4(and_4_out), .D5(and_3_out),
    .D6(and_2_out), .D7(and_1_out), .O0(O0), .O1(O1), .O2(O2), .O3(O3), .O4(O4), .O5(O5), .O6(O6), .O7(O7));
endmodule
