// Digital circuit CollectiveAnd56b.dig as structural Verilog
module CollectiveAnd56b (
  input  I0,
  input  I1,
  input  I2,
  input  I3,
  input  I4,
  input  I5,
  input  I6,
  input  I7,
  input  I8,
  input  I9,
  input  I10,
  input  I11,
  input  I12,
  input  I13,
  input  I14,
  input  I15,
  input  I16,
  input  I17,
  input  I18,
  input  I19,
  input  I20,
  input  I21,
  input  I22,
  input  I23,
  input  I24,
  input  I25,
  input  I26,
  input  I27,
  input  I28,
  input  I29,
  input  I30,
  input  I31,
  input  I32,
  input  I33,
  input  I34,
  input  I35,
  input  I36,
  input  I37,
  input  I38,
  input  I39,
  input  I40,
  input  I41,
  input  I42,
  input  I43,
  input  I44,
  input  I45,
  input  I46,
  input  I47,
  input  I48,
  input  I49,
  input  I50,
  input  I51,
  input  I52,
  input  I53,
  input  I54,
  input  I55,
  input  AND,
  output O0,
  output O1,
  output O2,
  output O3,
  output O4,
  output O5,
  output O6,
  output O7,
  output O8,
  output O9,
  output O10,
  output O11,
  output O12,
  output O13,
  output O14,
  output O15,
  output O16,
  output O17,
  output O18,
  output O19,
  output O20,
  output O21,
  output O22,
  output O23,
  output O24,
  output O25,
  output O26,
  output O27,
  output O28,
  output O29,
  output O30,
  output O31,
  output O32,
  output O33,
  output O34,
  output O35,
  output O36,
  output O37,
  output O38,
  output O39,
  output O40,
  output O41,
  output O42,
  output O43,
  output O44,
  output O45,
  output O46,
  output O47,
  output O48,
  output O49,
  output O50,
  output O51,
  output O52,
  output O53,
  output O54,
  output O55
);

  and and_1 (O0, I0, AND);
  and and_2 (O1, I1, AND);
  and and_3 (O2, I2, AND);
  and and_4 (O3, I3, AND);
  and and_5 (O4, I4, AND);
  and and_6 (O5, I5, AND);
  and and_7 (O6, I6, AND);
  and and_8 (O7, I7, AND);
  and and_9 (O8, I8, AND);
  and and_10 (O9, I9, AND);
  and and_11 (O10, I10, AND);
  and and_12 (O11, I11, AND);
  and and_13 (O12, I12, AND);
  and and_14 (O13, I13, AND);
  and and_15 (O14, I14, AND);
  and and_16 (O15, I15, AND);
  and and_17 (O16, I16, AND);
  and and_18 (O17, I17, AND);
  and and_19 (O18, I18, AND);
  and and_20 (O19, I19, AND);
  and and_21 (O20, I20, AND);
  and and_22 (O21, I21, AND);
  and and_23 (O22, I22, AND);
  and and_24 (O23, I23, AND);
  and and_25 (O24, I24, AND);
  and and_26 (O25, I25, AND);
  and and_27 (O26, I26, AND);
  and and_28 (O27, I27, AND);
  and and_29 (O28, I28, AND);
  and and_30 (O29, I29, AND);
  and and_31 (O30, I30, AND);
  and and_32 (O31, I31, AND);
  and and_33 (O32, I32, AND);
  and and_34 (O33, I33, AND);
  and and_35 (O34, I34, AND);
  and and_36 (O35, I35, AND);
  and and_37 (O36, I36, AND);
  and and_38 (O37, I37, AND);
  and and_39 (O38, I38, AND);
  and and_40 (O39, I39, AND);
  and and_41 (O40, I40, AND);
  and and_42 (O41, I41, AND);
  and and_43 (O42, I42, AND);
  and and_44 (O43, I43, AND);
  and and_45 (O44, I44, AND);
  and and_46 (O45, I45, AND);
  and and_47 (O46, I46, AND);
  and and_48 (O47, I47, AND);
  and and_49 (O48, I48, AND);
  and and_50 (O49, I49, AND);
  and and_51 (O50, I50, AND);
  and and_52 (O51, I51, AND);
  and and_53 (O52, I52, AND);
  and and_54 (O53, I53, AND);
  and and_55 (O54, I54, AND);
  and and_56 (O55, I55, AND);
endmodule
