// Digital circuit CollectiveAnd8b.dig as structural Verilog
module CollectiveAnd8b (
  input  I0,
  input  I1,
  input  I2,
  input  I3,
  input  I4,
  input  I5,
  input  I6,
  input  I7,
  input  AND,
  output O0,
  output O1,
  output O2,
  output O3,
  output O4,
  output O5,
  output O6,
  output O7
);

  and and_1 (O0, I0, AND);
  and and_2 (O1, I1, AND);
  and and_3 (O2, I2, AND);
  and and_4 (O3, I3, AND);
  and and_5 (O4, I4, AND);
  and and_6 (O5, I5, AND);
  and and_7 (O6, I6, AND);
  and and_8 (O7, I7, AND);
endmodule
