// Digital circuit Decrementer16b.dig as structural Verilog
module Decrementer16b (
  input  E,
  input  D0,
  input  D1,
  input  D2,
  input  D3,
  input  D4,
  input  D5,
  input  D6,
  input  D7,
  input  D8,
  input  D9,
  input  D10,
  input  D11,
  input  D12,
  input  D13,
  input  D14,
  input  D15,
  input  DEC,
  output O0,
  output O1,
  output O2,
  output O3,
  output O4,
  output O5,
  output O6,
  output O7,
  output O8,
  output O9,
  output O10,
  output O11,
  output O12,
  output O13,
  output O14,
  output O15,
  output CO
);

  wire full_adder_1_s, full_adder_2_co, full_adder_2_s, full_adder_3_co, full_adder_3_s, full_adder_4_co,
       full_adder_4_s, full_adder_5_co, full_adder_5_s, full_adder_6_co, full_adder_6_s, full_adder_7_co,
       full_adder_7_s, full_adder_8_co, full_adder_8_s, full_adder_9_co, full_adder_9_s, full_adder_10_co,
       full_adder_10_s, full_adder_11_co, full_adder_11_s, full_adder_12_co, full_adder_12_s,
       full_adder_13_co, full_adder_13_s, full_adder_14_co, full_adder_14_s, full_adder_15_co,
       full_adder_15_s, full_adder_16_co, full_adder_16_s, not_1_out;

  not not_1 (not_1_out, DEC);
  Full_Adder full_adder_1 (.X(D0), .Y(1'b1), .C(full_adder_2_co), .S(full_adder_1_s), .CO(CO));
  Full_Adder full_adder_2 (.X(D1), .Y(1'b1), .C(full_adder_3_co), .S(full_adder_2_s), .CO(full_adder_2_co));
  Full_Adder full_adder_3 (.X(D2), .Y(1'b1), .C(full_adder_4_co), .S(full_adder_3_s), .CO(full_adder_3_co));
  Full_Adder full_adder_4 (.X(D3), .Y(1'b1), .C(full_adder_5_co), .S(full_adder_4_s), .CO(full_adder_4_co));
  Full_Adder full_adder_5 (.X(D4), .Y(1'b1), .C(full_adder_6_co), .S(full_adder_5_s), .CO(full_adder_5_co));
  Full_Adder full_adder_6 (.X(D5), .Y(1'b1), .C(full_adder_7_co), .S(full_adder_6_s), .CO(full_adder_6_co));
  Full_Adder full_adder_7 (.X(D6), .Y(1'b1), .C(full_adder_8_co), .S(full_adder_7_s), .CO(full_adder_7_co));
  Full_Adder full_adder_8 (.X(D7), .Y(1'b1), .C(full_adder_9_co), .S(full_adder_8_s), .CO(full_adder_8_co));
  Full_Adder full_adder_9 (.X(D8), .Y(1'b1), .C(full_adder_10_co), .S(full_adder_9_s), .CO(full_adder_9_co));
  Full_Adder full_adder_10 (.X(D9), .Y(1'b1), .C(full_adder_11_co), .S(full_adder_10_s), .CO(full_adder_10_co));
  Full_Adder full_adder_11 (.X(D10), .Y(1'b1), .C(full_adder_12_co), .S(full_adder_11_s), .CO(full_adder_11_co));
  Full_Adder full_adder_12 (.X(D11), .Y(1'b1), .C(full_adder_13_co), .S(full_adder_12_s), .CO(full_adder_12_co));
  Full_Adder full_adder_13 (.X(D12), .Y(1'b1), .C(full_adder_14_co), .S(full_adder_13_s), .CO(full_adder_13_co));
  Full_Adder full_adder_14 (.X(D13), .Y(1'b1), .C(full_adder_15_co), .S(full_adder_14_s), .CO(full_adder_14_co));
  Full_Adder full_adder_15 (.X(D14), .Y(1'b1), .C(full_adder_16_co), .S(full_adder_15_s), .CO(full_adder_15_co));
  Full_Adder full_adder_16 (.X(D15), .Y(1'b1), .C(not_1_out), .S(full_adder_16_s), .CO(full_adder_16_co));
  assign O0 = E ? full_adder_1_s : 1'bz;  // Driver driver_1
  assign O1 = E ? full_adder_2_s : 1'bz;  // Driver driver_2
  assign O2 = E ? full_adder_3_s : 1'bz;  // Driver driver_3
  assign O3 = E ? full_adder_4_s : 1'bz;  // Driver driver_4
  assign O4 = E ? full_adder_5_s : 1'bz;  // Driver driver_5
  assign O5 = E ? full_adder_6_s : 1'bz;  // Driver driver_6
  assign O6 = E ? full_adder_7_s : 1'bz;  // Driver driver_7
  assign O7 = E ? full_adder_8_s : 1'bz;  // Driver driver_8
  assign O8 = E ? full_adder_9_s : 1'bz;  // Driver driver_9
  assign O9 = E ? full_adder_10_s : 1'bz;  // Driver driver_10
  assign O10 = E ? full_adder_11_s : 1'bz;  // Driver driver_11
  assign O11 = E ? full_adder_12_s : 1'bz;  // Driver driver_12
  assign O12 = E ? full_adder_13_s : 1'bz;  // Driver driver_13
  assign O13 = E ? full_adder_14_s : 1'bz;  // Driver driver_14
  assign O14 = E ? full_adder_15_s : 1'bz;  // Driver driver_15
  assign O15 = E ? full_adder_16_s : 1'bz;  // Driver driver_16
endmodule
