// Digital circuit Full Adder.dig as structural Verilog
module Full_Adder (
  input  X,
  input  Y,
  input  C,
  output S,
  output CO
);

  wire and_1_out, and_2_out, xor_1_out;

  xor xor_1 (xor_1_out, X, Y);
  xor xor_2 (S, xor_1_out, C);
  and and_1 (and_1_out, C, xor_1_out);
  and and_2 (and_2_out, X, Y);
  or or_1 (CO, and_1_out, and_2_out);
endmodule
