// Digital circuit Incrementer.dig as structural Verilog
module Incrementer (
  input  E,
  input  D0,
  input  D1,
  input  D2,
  input  D3,
  input  D4,
  input  D5,
  input  D6,
  input  D7,
  output O0,
  output O1,
  output O2,
  output O3,
  output O4,
  output O5,
  output O6,
  output O7
);

  wire full_adder_1_co, full_adder_1_s, full_adder_2_co, full_adder_2_s, full_adder_3_co, full_adder_3_s,
       full_adder_4_co, full_adder_4_s, full_adder_5_co, full_adder_5_s, full_adder_6_co, full_adder_6_s,
       full_adder_7_co, full_adder_7_s, full_adder_8_co, full_adder_8_s;

  Full_Adder full_adder_1 (.X(D0), .Y(1'b0), .C(1'b1), .S(full_adder_1_s), .CO(full_adder_1_co));
  Full_Adder full_adder_2 (.X(D1), .Y(1'b0), .C(full_adder_1_co), .S(full_adder_2_s), .CO(full_adder_2_co));
  Full_Adder full_adder_3 (.X(D2), .Y(1'b0), .C(full_adder_2_co), .S(full_adder_3_s), .CO(full_adder_3_co));
  Full_Adder full_adder_4 (.X(D3), .Y(1'b0), .C(full_adder_3_co), .S(full_adder_4_s), .CO(full_adder_4_co));
  Full_Adder full_adder_5 (.X(D4), .Y(1'b0), .C(full_adder_4_co), .S(full_adder_5_s), .CO(full_adder_5_co));
  Full_Adder full_adder_6 (.X(D5), .Y(1'b0), .C(full_adder_5_co), .S(full_adder_6_s), .CO(full_adder_6_co));
  Full_Adder full_adder_7 (.X(D6), .Y(1'b0), .C(full_adder_6_co), .S(full_adder_7_s), .CO(full_adder_7_co));
  Full_Adder full_adder_8 (.X(D7), .Y(1'b0), .C(full_adder_7_co), .S(full_adder_8_s), .CO(full_adder_8_co));
  LED led_1 (.in(full_adder_8_co));
  assign O0 = E ? full_adder_1_s : 1'bz;  // Driver driver_1
  assign O1 = E ? full_adder_2_s : 1'bz;  // Driver driver_2
  assign O2 = E ? full_adder_3_s : 1'bz;  // Driver driver_3
  assign O3 = E ? full_adder_4_s : 1'bz;  // Driver driver_4
  assign O4 = E ? full_adder_5_s : 1'bz;  // Driver driver_5
  assign O5 = E ? full_adder_6_s : 1'bz;  // Driver driver_6
  assign O6 = E ? full_adder_7_s : 1'bz;  // Driver driver_7
  assign O7 = E ? full_adder_8_s : 1'bz;  // Driver driver_8
endmodule
