// Digital circuit Multiplier8b.dig as structural Verilog
module Multiplier8b (
  input  E,
  input  X0,
  input  X1,
  input  X2,
  input  X3,
  input  X4,
  input  X5,
  input  X6,
  input  X7,
  input  Y0,
  input  Y1,
  input  Y2,
  input  Y3,
  input  Y4,
  input  Y5,
  input  Y6,
  input  Y7,
  output O0,
  output O1,
  output O2,
  output O3,
  output O4,
  output O5,
  output O6,
  output O7,
  output O8,
  output O9,
  output O10,
  output O11,
  output O12,
  output O13,
  output O14,
  output O15,
  output F0,
  output FO
);

  wire adder8b_1_p11, adder8b_1_p13, adder8b_1_p15, adder8b_1_p17, adder8b_1_p19, adder8b_1_p21,
       adder8b_1_p23, adder8b_1_p25, adder8b_1_p27, adder8b_2_p11, adder8b_2_p13, adder8b_2_p15,
       adder8b_2_p17, adder8b_2_p19, adder8b_2_p21, adder8b_2_p23, adder8b_2_p25, adder8b_2_p27,
       adder8b_3_p11, adder8b_3_p13, adder8b_3_p15, adder8b_3_p17, adder8b_3_p19, adder8b_3_p21,
       adder8b_3_p23, adder8b_3_p25, adder8b_3_p27, adder8b_4_p11, adder8b_4_p13, adder8b_4_p15,
       adder8b_4_p17, adder8b_4_p19, adder8b_4_p21, adder8b_4_p23, adder8b_4_p25, adder8b_4_p27,
       adder8b_5_p11, adder8b_5_p13, adder8b_5_p15, adder8b_5_p17, adder8b_5_p19, adder8b_5_p21,
       adder8b_5_p23, adder8b_5_p25, adder8b_5_p27, adder8b_6_p11, adder8b_6_p13, adder8b_6_p15,
       adder8b_6_p17, adder8b_6_p19, adder8b_6_p21, adder8b_6_p23, adder8b_6_p25, adder8b_6_p27,
       adder8b_7_p20, adder8b_7_p22, adder8b_7_p24, adder8b_7_p26, adder8b_7_p28, adder8b_7_p30,
       adder8b_7_p32, adder8b_7_p34, adder8b_7_p36, collectiveand8b_1_o0, collectiveand8b_1_o1,
       collectiveand8b_1_o2, collectiveand8b_1_o3, collectiveand8b_1_o4, collectiveand8b_1_o5,
       collectiveand8b_1_o6, collectiveand8b_1_o7, collectiveand8b_2_o0, collectiveand8b_2_o1,
       collectiveand8b_2_o2, collectiveand8b_2_o3, collectiveand8b_2_o4, collectiveand8b_2_o5,
       collectiveand8b_2_o6, collectiveand8b_2_o7, collectiveand8b_3_o0, collectiveand8b_3_o1,
       collectiveand8b_3_o2, collectiveand8b_3_o3, collectiveand8b_3_o4, collectiveand8b_3_o5,
       collectiveand8b_3_o6, collectiveand8b_3_o7, collectiveand8b_4_o0, collectiveand8b_4_o1,
       collectiveand8b_4_o2, collectiveand8b_4_o3, collectiveand8b_4_o4, collectiveand8b_4_o5,
       collectiveand8b_4_o6, collectiveand8b_4_o7, collectiveand8b_5_o0, collectiveand8b_5_o1,
       collectiveand8b_5_o2, collectiveand8b_5_o3, collectiveand8b_5_o4, collectiveand8b_5_o5,
       collectiveand8b_5_o6, collectiveand8b_5_o7, collectiveand8b_6_o0, collectiveand8b_6_o1,
       collectiveand8b_6_o2, collectiveand8b_6_o3, collectiveand8b_6_o4, collectiveand8b_6_o5,
       collectiveand8b_6_o6, collectiveand8b_6_o7, collectiveand8b_7_o0, collectiveand8b_7_o1,
       collectiveand8b_7_o2, collectiveand8b_7_o3, collectiveand8b_7_o4, collectiveand8b_7_o5,
       collectiveand8b_7_o6, collectiveand8b_7_o7, collectiveand8b_8_o0, collectiveand8b_8_o1,
       collectiveand8b_8_o2, collectiveand8b_8_o3, collectiveand8b_8_o4, collectiveand8b_8_o5,
       collectiveand8b_8_o6, collectiveand8b_8_o7;

  CollectiveAnd8b collectiveand8b_1 (
    .I0(X0), .I1(X1), .I2(X2), .I3(X3), .I4(X4), .I5(X5), .I6(X6), .I7(X7), .AND(Y6),
    .O0(collectiveand8b_1_o0), .O1(collectiveand8b_1_o1), .O2(collectiveand8b_1_o2),
    .O3(collectiveand8b_1_o3), .O4(collectiveand8b_1_o4), .O5(collectiveand8b_1_o5),
    .O6(collectiveand8b_1_o6), .O7(collectiveand8b_1_o7));
  CollectiveAnd8b collectiveand8b_2 (
    .I0(X0), .I1(X1), .I2(X2), .I3(X3), .I4(X4), .I5(X5), .I6(X6), .I7(X7), .AND(Y5),
    .O0(collectiveand8b_2_o0), .O1(collectiveand8b_2_o1), .O2(collectiveand8b_2_o2),
    .O3(collectiveand8b_2_o3), .O4(collectiveand8b_2_o4), .O5(collectiveand8b_2_o5),
    .O6(collectiveand8b_2_o6), .O7(collectiveand8b_2_o7));
  CollectiveAnd8b collectiveand8b_3 (
    .I0(X0), .I1(X1), .I2(X2), .I3(X3), .I4(X4), .I5(X5), .I6(X6), .I7(X7), .AND(Y4),
    .O0(collectiveand8b_3_o0), .O1(collectiveand8b_3_o1), .O2(collectiveand8b_3_o2),
    .O3(collectiveand8b_3_o3), .O4(collectiveand8b_3_o4), .O5(collectiveand8b_3_o5),
    .O6(collectiveand8b_3_o6), .O7(collectiveand8b_3_o7));
  CollectiveAnd8b collectiveand8b_4 (
    .I0(X0), .I1(X1), .I2(X2), .I3(X3), .I4(X4), .I5(X5), .I6(X6), .I7(X7), .AND(Y3),
    .O0(collectiveand8b_4_o0), .O1(collectiveand8b_4_o1), .O2(collectiveand8b_4_o2),
    .O3(collectiveand8b_4_o3), .O4(collectiveand8b_4_o4), .O5(collectiveand8b_4_o5),
    .O6(collectiveand8b_4_o6), .O7(collectiveand8b_4_o7));
  CollectiveAnd8b collectiveand8b_5 (
    .I0(X0), .I1(X1), .I2(X2), .I3(X3), .I4(X4), .I5(X5), .I6(X6), .I7(X7), .AND(Y2),
    .O0(collectiveand8b_5_o0), .O1(collectiveand8b_5_o1), .O2(collectiveand8b_5_o2),
    .O3(collectiveand8b_5_o3), .O4(collectiveand8b_5_o4), .O5(collectiveand8b_5_o5),
    .O6(collectiveand8b_5_o6), .O7(collectiveand8b_5_o7));
  CollectiveAnd8b collectiveand8b_6 (
    .I0(X0), .I1(X1), .I2(X2), .I3(X3), .I4(X4), .I5(X5), .I6(X6), .I7(X7), .AND(Y1),
    .O0(collectiveand8b_6_o0), .O1(collectiveand8b_6_o1), .O2(collectiveand8b_6_o2),
    .O3(collectiveand8b_6_o3), .O4(collectiveand8b_6_o4), .O5(collectiveand8b_6_o5),
    .O6(collectiveand8b_6_o6), .O7(collectiveand8b_6_o7));
  CollectiveAnd8b collectiveand8b_7 (
    .I0(X0), .I1(X1), .I2(X2), .I3(X3), .I4(X4), .I5(X5), .I6(X6), .I7(X7), .AND(Y0),
    .O0(collectiveand8b_7_o0), .O1(collectiveand8b_7_o1), .O2(collectiveand8b_7_o2),
    .O3(collectiveand8b_7_o3), .O4(collectiveand8b_7_o4), .O5(collectiveand8b_7_o5),
    .O6(collectiveand8b_7_o6), .O7(collectiveand8b_7_o7));
  CollectiveAnd8b collectiveand8b_8 (
    .I0(X0), .I1(X1), .I2(X2), .I3(X3), .I4(X4), .I5(X5), .I6(X6), .I7(X7), .AND(Y7),
    .O0(collectiveand8b_8_o0), .O1(collectiveand8b_8_o1), .O2(collectiveand8b_8_o2),
    .O3(collectiveand8b_8_o3), .O4(collectiveand8b_8_o4), .O5(collectiveand8b_8_o5),
    .O6(collectiveand8b_8_o6), .O7(collectiveand8b_8_o7));
  // Adder8b adder8b_1: pin names not known; wires that end beside it: 1'b0, collectiveand8b_1_o7, collectiveand8b_1_o6, collectiveand8b_1_o5, collectiveand8b_1_o4, collectiveand8b_1_o3, collectiveand8b_1_o2, collectiveand8b_1_o1, collectiveand8b_1_o0, collectiveand8b_8_o6, adder8b_1_p11, collectiveand8b_8_o5, adder8b_1_p13, collectiveand8b_8_o4, adder8b_1_p15, collectiveand8b_8_o3, adder8b_1_p17, collectiveand8b_8_o2, adder8b_1_p19, collectiveand8b_8_o1, adder8b_1_p21, collectiveand8b_8_o0, adder8b_1_p23, 1'b0, adder8b_1_p25, 1'b1, adder8b_1_p27
  // Adder8b adder8b_2: pin names not known; wires that end beside it: 1'b0, collectiveand8b_2_o7, collectiveand8b_2_o6, collectiveand8b_2_o5, collectiveand8b_2_o4, collectiveand8b_2_o3, collectiveand8b_2_o2, collectiveand8b_2_o1, collectiveand8b_2_o0, adder8b_1_p13, adder8b_2_p11, adder8b_1_p15, adder8b_2_p13, adder8b_1_p17, adder8b_2_p15, adder8b_1_p19, adder8b_2_p17, adder8b_1_p21, adder8b_2_p19, adder8b_1_p23, adder8b_2_p21, adder8b_1_p25, adder8b_2_p23, adder8b_1_p27, adder8b_2_p25, 1'b1, adder8b_2_p27
  // Adder8b adder8b_3: pin names not known; wires that end beside it: 1'b0, collectiveand8b_3_o7, collectiveand8b_3_o6, collectiveand8b_3_o5, collectiveand8b_3_o4, collectiveand8b_3_o3, collectiveand8b_3_o2, collectiveand8b_3_o1, collectiveand8b_3_o0, adder8b_2_p13, adder8b_3_p11, adder8b_2_p15, adder8b_3_p13, adder8b_2_p17, adder8b_3_p15, adder8b_2_p19, adder8b_3_p17, adder8b_2_p21, adder8b_3_p19, adder8b_2_p23, adder8b_3_p21, adder8b_2_p25, adder8b_3_p23, adder8b_2_p27, adder8b_3_p25, 1'b1, adder8b_3_p27
  // Adder8b adder8b_4: pin names not known; wires that end beside it: 1'b0, collectiveand8b_4_o7, collectiveand8b_4_o6, collectiveand8b_4_o5, collectiveand8b_4_o4, collectiveand8b_4_o3, collectiveand8b_4_o2, collectiveand8b_4_o1, collectiveand8b_4_o0, adder8b_3_p13, adder8b_4_p11, adder8b_3_p15, adder8b_4_p13, adder8b_3_p17, adder8b_4_p15, adder8b_3_p19, adder8b_4_p17, adder8b_3_p21, adder8b_4_p19, adder8b_3_p23, adder8b_4_p21, adder8b_3_p25, adder8b_4_p23, adder8b_3_p27, adder8b_4_p25, 1'b1, adder8b_4_p27
  // Adder8b adder8b_5: pin names not known; wires that end beside it: 1'b0, collectiveand8b_5_o7, collectiveand8b_5_o6, collectiveand8b_5_o5, collectiveand8b_5_o4, collectiveand8b_5_o3, collectiveand8b_5_o2, collectiveand8b_5_o1, collectiveand8b_5_o0, adder8b_4_p13, adder8b_5_p11, adder8b_4_p15, adder8b_5_p13, adder8b_4_p17, adder8b_5_p15, adder8b_4_p19, adder8b_5_p17, adder8b_4_p21, adder8b_5_p19, adder8b_4_p23, adder8b_5_p21, adder8b_4_p25, adder8b_5_p23, adder8b_4_p27, adder8b_5_p25, 1'b1, adder8b_5_p27
  // Adder8b adder8b_6: pin names not known; wires that end beside it: 1'b0, collectiveand8b_6_o7, collectiveand8b_6_o6, collectiveand8b_6_o5, collectiveand8b_6_o4, collectiveand8b_6_o3, collectiveand8b_6_o2, collectiveand8b_6_o1, collectiveand8b_6_o0, adder8b_5_p13, adder8b_6_p11, adder8b_5_p15, adder8b_6_p13, adder8b_5_p17, adder8b_6_p15, adder8b_5_p19, adder8b_6_p17, adder8b_5_p21, adder8b_6_p19, adder8b_5_p23, adder8b_6_p21, adder8b_5_p25, adder8b_6_p23, adder8b_5_p27, adder8b_6_p25, 1'b1, adder8b_6_p27
  // Adder8b adder8b_7: pin names not known; wires that end beside it: Y0, X7, X6, X5, X4, X3, X2, X1, X0, 1'b0, collectiveand8b_7_o7, collectiveand8b_7_o6, collectiveand8b_7_o5, collectiveand8b_7_o4, collectiveand8b_7_o3, collectiveand8b_7_o2, collectiveand8b_7_o1, collectiveand8b_7_o0, adder8b_6_p13, adder8b_7_p20, adder8b_6_p15, adder8b_7_p22, adder8b_6_p17, adder8b_7_p24, adder8b_6_p19, adder8b_7_p26, adder8b_6_p21, adder8b_7_p28, adder8b_6_p23, adder8b_7_p30, adder8b_6_p25, adder8b_7_p32, adder8b_6_p27, adder8b_7_p34, 1'b1, adder8b_7_p36, collectiveand8b_8_o7, adder8b_1_p11, adder8b_2_p11, adder8b_3_p11, adder8b_4_p11, adder8b_5_p11, adder8b_6_p11, adder8b_7_p20, adder8b_7_p22, adder8b_7_p24, adder8b_7_p26, adder8b_7_p28, adder8b_7_p30
  assign O0 = E ? adder8b_7_p36 : 1'bz;  // Driver driver_1
  assign O1 = E ? adder8b_7_p34 : 1'bz;  // Driver driver_2
  assign O2 = E ? adder8b_7_p32 : 1'bz;  // Driver driver_3
  assign O3 = E ? adder8b_7_p30 : 1'bz;  // Driver driver_4
  assign O4 = E ? adder8b_7_p28 : 1'bz;  // Driver driver_5
  assign O5 = E ? adder8b_7_p26 : 1'bz;  // Driver driver_6
  assign O6 = E ? adder8b_7_p24 : 1'bz;  // Driver driver_7
  assign O7 = E ? adder8b_7_p22 : 1'bz;  // Driver driver_8
  assign O8 = E ? adder8b_7_p20 : 1'bz;  // Driver driver_9
  assign O9 = E ? adder8b_6_p11 : 1'bz;  // Driver driver_10
  assign O10 = E ? adder8b_5_p11 : 1'bz;  // Driver driver_11
  assign O11 = E ? adder8b_4_p11 : 1'bz;  // Driver driver_12
  assign O12 = E ? adder8b_3_p11 : 1'bz;  // Driver driver_13
  assign O13 = E ? adder8b_2_p11 : 1'bz;  // Driver driver_14
  assign O14 = E ? adder8b_1_p11 : 1'bz;  // Driver driver_15
  assign O15 = E ? collectiveand8b_8_o7 : 1'bz;  // Driver driver_16
endmodule
