// Digital circuit Not8b.dig as structural Verilog
module Not8b (
  input  E,
  input  D0,
  input  D1,
  input  D2,
  input  D3,
  input  D4,
  input  D5,
  input  D6,
  input  D7,
  output O0,
  output O1,
  output O2,
  output O3,
  output O4,
  output O5,
  output O6,
  output O7
);

  wire not_1_out, not_2_out, not_3_out, not_4_out, not_5_out, not_6_out, not_7_out, not_8_out;

  not not_1 (not_1_out, D0);
  not not_2 (not_2_out, D1);
  not not_3 (not_3_out, D2);
  not not_4 (not_4_out, D3);
  not not_5 (not_5_out, D4);
  not not_6 (not_6_out, D5);
  not not_7 (not_7_out, D6);
  not not_8 (not_8_out, D7);
  assign O0 = E ? not_1_out : 1'bz;  // Driver driver_1
  assign O1 = E ? not_2_out : 1'bz;  // Driver driver_2
  assign O2 = E ? not_3_out : 1'bz;  // Driver driver_3
  assign O3 = E ? not_4_out : 1'bz;  // Driver driver_4
  assign O4 = E ? not_5_out : 1'bz;  // Driver driver_5
  assign O5 = E ? not_6_out : 1'bz;  // Driver driver_6
  assign O6 = E ? not_7_out : 1'bz;  // Driver driver_7
  assign O7 = E ? not_8_out : 1'bz;  // Driver driver_8
endmodule
