// Digital circuit Or8b.dig as structural Verilog
module Or8b (
  input  E,
  input  X0,
  input  X1,
  input  X2,
  input  X3,
  input  X4,
  input  X5,
  input  X6,
  input  X7,
  input  Y0,
  input  Y1,
  input  Y2,
  input  Y3,
  input  Y4,
  input  Y5,
  input  Y6,
  input  Y7,
  output O0,
  output O1,
  output O2,
  output O3,
  output O4,
  output O5,
  output O6,
  output O7
);

  wire or_1_out, or_2_out, or_3_out, or_4_out, or_5_out, or_6_out, or_7_out, or_8_out;

  or or_1 (or_1_out, X7, Y7);
  or or_2 (or_2_out, X6, Y6);
  or or_3 (or_3_out, X5, Y5);
  or or_4 (or_4_out, X4, Y4);
  or or_5 (or_5_out, X3, Y3);
  or or_6 (or_6_out, X2, Y2);
  or or_7 (or_7_out, X1, Y1);
  or or_8 (or_8_out, X0, Y0);
  PinControl8b pincontrol8b_1 (
    .E(E), .D0(or_8_out), .D1(or_7_out), .D2(or_6_out), .D3(or_5_out), .D4(or_4_out), .D5(or_3_out),
    .D6(or_2_out), .D7(or_1_out), .O0(O0), .O1(O1), .O2(O2), .O3(O3), .O4(O4), .O5(O5), .O6(O6), .O7(O7));
endmodule
