// Digital circuit ShiftRight8b.dig as structural Verilog
module ShiftRight8b (
  input  E,
  input  D0,
  input  D1,
  input  D2,
  input  D3,
  input  D4,
  input  D5,
  input  D6,
  input  D7,
  output O0,
  output O1,
  output O2,
  output O3,
  output O4,
  output O5,
  output O6,
  output O7,
  output C
);

  assign O0 = E ? 1'b0 : 1'bz;  // Driver driver_1
  assign O1 = E ? D0 : 1'bz;  // Driver driver_2
  assign O2 = E ? D1 : 1'bz;  // Driver driver_3
  assign O3 = E ? D2 : 1'bz;  // Driver driver_4
  assign O4 = E ? D3 : 1'bz;  // Driver driver_5
  assign O5 = E ? D4 : 1'bz;  // Driver driver_6
  assign O6 = E ? D5 : 1'bz;  // Driver driver_7
  assign O7 = E ? D6 : 1'bz;  // Driver driver_8
  assign C = E ? D7 : 1'bz;  // Driver driver_9
endmodule
