// Digital circuit Xor8b.dig as structural Verilog
module Xor8b (
  input  E,
  input  X0,
  input  X1,
  input  X2,
  input  X3,
  input  X4,
  input  X5,
  input  X6,
  input  X7,
  input  Y0,
  input  Y1,
  input  Y2,
  input  Y3,
  input  Y4,
  input  Y5,
  input  Y6,
  input  Y7,
  output O0,
  output O1,
  output O2,
  output O3,
  output O4,
  output O5,
  output O6,
  output O7
);

  wire xor_1_out, xor_2_out, xor_3_out, xor_4_out, xor_5_out, xor_6_out, xor_7_out, xor_8_out;

  xor xor_1 (xor_1_out, X7, Y7);
  xor xor_2 (xor_2_out, X6, Y6);
  xor xor_3 (xor_3_out, X5, Y5);
  xor xor_4 (xor_4_out, X4, Y4);
  xor xor_5 (xor_5_out, X3, Y3);
  xor xor_6 (xor_6_out, X2, Y2);
  xor xor_7 (xor_7_out, X1, Y1);
  xor xor_8 (xor_8_out, X0, Y0);
  PinControl8b pincontrol8b_1 (
    .E(E), .D0(xor_8_out), .D1(xor_7_out), .D2(xor_6_out), .D3(xor_5_out), .D4(xor_4_out), .D5(xor_3_out),
    .D6(xor_2_out), .D7(xor_1_out), .O0(O0), .O1(O1), .O2(O2), .O3(O3), .O4(O4), .O5(O5), .O6(O6), .O7(O7));
endmodule
