// Digital circuit Clock.dig as structural Verilog
module Clock (
  input  HLT,
  input  Clock,
  input  M_CLK,
  input  M_E,
  output CLK
);

  wire and_1_out, and_2_out, not_1_out, not_2_out, or_1_out;

  not not_1 (not_1_out, M_E);
  and and_1 (and_1_out, not_1_out, Clock);
  and and_2 (and_2_out, M_CLK, M_E);
  not not_2 (not_2_out, HLT);
  or or_1 (or_1_out, and_1_out, and_2_out);
  and and_3 (CLK, not_2_out, or_1_out);
endmodule
