// Digital circuit D-Latch.dig as structural Verilog
module D_Latch (
  input  D,
  input  E,
  output OUT
);

  wire and_1_out, and_2_out, nor_2_out, not_1_out;

  not not_1 (not_1_out, D);
  and and_1 (and_1_out, not_1_out, E);
  and and_2 (and_2_out, D, E);
  nor nor_1 (OUT, and_1_out, nor_2_out);
  nor nor_2 (nor_2_out, OUT, and_2_out);
endmodule
