// Digital circuit IOHandler.dig as structural Verilog
module IOHandler (
  input  D0,
  input  D1,
  input  D2,
  input  D3,
  input  D4,
  input  D5,
  input  D6,
  input  D7,
  input  A0,
  input  A1,
  input  A2,
  input  A3,
  input  A4,
  input  A5,
  input  A6,
  input  A7,
  input  CLK,
  input  E,
  input  R,
  input  W,
  output AD0,
  output AD1,
  output AD2,
  output AD3,
  output AD4,
  output AD5,
  output AD6,
  output AD7,
  output BD0,
  output BD1,
  output BD2,
  output BD3,
  output BD4,
  output BD5,
  output BD6,
  output BD7
);

  wire and_1_out, and_2_out, and_3_out, and_4_out, and_5_out, nand_1_out, nand_2_out, not_1_out, not_2_out,
       Peripheral_Control_o0, Peripheral_Control_o1, Peripheral_Control_o2, Peripheral_Control_o3,
       Peripheral_Control_o4, Peripheral_Control_o5, Peripheral_Control_o6, Peripheral_Control_o7,
       pincontrol8b_1_o0, pincontrol8b_1_o1, pincontrol8b_1_o2, pincontrol8b_1_o3, pincontrol8b_1_o4,
       pincontrol8b_1_o5, pincontrol8b_1_o6, pincontrol8b_1_o7, pincontrol8b_2_o0, pincontrol8b_2_o1,
       pincontrol8b_2_o2, pincontrol8b_2_o3, pincontrol8b_2_o4, pincontrol8b_2_o5, pincontrol8b_2_o6,
       pincontrol8b_2_o7, undriven;

  and and_1 (and_1_out, CLK, E);
  nand nand_1 (nand_1_out, A0, A1, A2, A3, A4);
  and and_2 (and_2_out, A0, ~A1, ~A2, A3, ~A4, ~A5, ~A6, ~A7);  // And
  PinControl8b pincontrol8b_1 (
    .E(not_1_out), .D0(D0), .D1(D1), .D2(D2), .D3(D3), .D4(D4), .D5(D5), .D6(D6), .D7(D7),
    .O0(pincontrol8b_1_o0), .O1(pincontrol8b_1_o1), .O2(pincontrol8b_1_o2), .O3(pincontrol8b_1_o3),
    .O4(pincontrol8b_1_o4), .O5(pincontrol8b_1_o5), .O6(pincontrol8b_1_o6), .O7(pincontrol8b_1_o7));
  and and_3 (and_3_out, ~A0, A1, ~A2, A3, ~A4, ~A5, ~A6, ~A7);  // And
  PinControl8b pincontrol8b_2 (
    .E(not_2_out), .D0(D0), .D1(D1), .D2(D2), .D3(D3), .D4(D4), .D5(D5), .D6(D6), .D7(D7),
    .O0(pincontrol8b_2_o0), .O1(pincontrol8b_2_o1), .O2(pincontrol8b_2_o2), .O3(pincontrol8b_2_o3),
    .O4(pincontrol8b_2_o4), .O5(pincontrol8b_2_o5), .O6(pincontrol8b_2_o6), .O7(pincontrol8b_2_o7));
  nand nand_2 (nand_2_out, A0, A1, A2, A3, A4, A5, A6, A7);
  not not_1 (not_1_out, Peripheral_Control_o0);
  not not_2 (not_2_out, Peripheral_Control_o4);
  and and_4 (and_4_out, and_1_out, nand_1_out);
  PinControl8b pincontrol8b_3 (
    .E(Peripheral_Control_o0), .D0(AD0), .D1(AD1), .D2(AD2), .D3(AD3), .D4(AD4), .D5(AD5), .D6(AD6),
    .D7(AD7), .O0(pincontrol8b_1_o0), .O1(pincontrol8b_1_o1), .O2(pincontrol8b_1_o2), .O3(pincontrol8b_1_o3),
    .O4(pincontrol8b_1_o4), .O5(pincontrol8b_1_o5), .O6(pincontrol8b_1_o6), .O7(pincontrol8b_1_o7));
  PinControl8b pincontrol8b_4 (
    .E(Peripheral_Control_o4), .D0(BD0), .D1(BD1), .D2(BD2), .D3(BD3), .D4(BD4), .D5(BD5), .D6(BD6),
    .D7(undriven), .O0(pincontrol8b_2_o0), .O1(pincontrol8b_2_o1), .O2(pincontrol8b_2_o2),
    .O3(pincontrol8b_2_o3), .O4(pincontrol8b_2_o4), .O5(pincontrol8b_2_o5), .O6(pincontrol8b_2_o6),
    .O7(pincontrol8b_2_o7));
  Register Peripheral_Control (
    .CLK(and_1_out), .E(nand_2_out), .R(1'b1), .W(W), .D0(D0), .D1(D1), .D2(D2), .D3(D3), .D4(D4), .D5(D5),
    .D6(D6), .D7(D7), .O0(Peripheral_Control_o0), .O1(Peripheral_Control_o1), .O2(Peripheral_Control_o2),
    .O3(Peripheral_Control_o3), .O4(Peripheral_Control_o4), .O5(Peripheral_Control_o5),
    .O6(Peripheral_Control_o6), .O7(Peripheral_Control_o7));
  RAMDualPort #(.AddrBits(3), .Bits(8)) Device_Address (
    .A({A2, A1, A0}), .Din({D7, D6, D5, D4, D3, D2, D1, D0}), .str(W), .C(and_4_out), .ld(R),
    .D({D7, D6, D5, D4, D3, D2, D1, D0}));
  Register A_Buffer (
    .CLK(and_1_out), .E(and_2_out), .R(R), .W(W), .D0(pincontrol8b_1_o0), .D1(pincontrol8b_1_o1),
    .D2(pincontrol8b_1_o2), .D3(pincontrol8b_1_o3), .D4(pincontrol8b_1_o4), .D5(pincontrol8b_1_o5),
    .D6(pincontrol8b_1_o6), .D7(pincontrol8b_1_o7), .O0(D0), .O1(D1), .O2(D2), .O3(D3), .O4(D4), .O5(D5),
    .O6(D6), .O7(D7));
  Register B_Buffer (
    .CLK(and_1_out), .E(and_3_out), .R(R), .W(W), .D0(pincontrol8b_2_o0), .D1(pincontrol8b_2_o1),
    .D2(pincontrol8b_2_o2), .D3(pincontrol8b_2_o3), .D4(pincontrol8b_2_o4), .D5(pincontrol8b_2_o5),
    .D6(pincontrol8b_2_o6), .D7(pincontrol8b_2_o7), .O0(D0), .O1(D1), .O2(D2), .O3(D3), .O4(D4), .O5(D5),
    .O6(D6), .O7(D7));
  and and_5 (and_5_out, R, nand_2_out);
  PinControl8b pincontrol8b_5 (
    .E(and_5_out), .D0(Peripheral_Control_o0), .D1(Peripheral_Control_o1), .D2(Peripheral_Control_o2),
    .D3(Peripheral_Control_o3), .D4(Peripheral_Control_o4), .D5(Peripheral_Control_o5),
    .D6(Peripheral_Control_o6), .D7(Peripheral_Control_o7), .O0(D0), .O1(D1), .O2(D2), .O3(D3), .O4(D4),
    .O5(D5), .O6(D6), .O7(D7));
  // Pins of 3 and 8 bits meet at {A7, A6, A5, A4, A3, A2, A1, A0}

  // Notes on the sheet:
  //   R/W
endmodule
