// Digital circuit Instruction Decoder.dig as structural Verilog
module Instruction_Decoder (
  input  CLK,
  input  I0,
  input  I1,
  input  I2,
  input  I3,
  input  I4,
  input  I5,
  input  I6,
  input  I7,
  input  IRQ,
  input  INT,
  input  F0,
  input  FC,
  input  FO,
  input  FN,
  output D0,
  output D1,
  output D2,
  output D3,
  output D4,
  output D5,
  output D6,
  output D7,
  output ALUE,
  output ALU_B,
  output ALUC,
  output ALUADD,
  output ALUAND,
  output ALUOR,
  output ALUNOT,
  output ALUXOR,
  output ALUSL,
  output ALUSR,
  output ALURL,
  output ALURR,
  output AR,
  output AW,
  output XR,
  output XW,
  output YR,
  output YW,
  output ZR,
  output ZW,
  output PCE,
  output PCHR,
  output PCHW,
  output PCLR,
  output PCLW,
  output SPR,
  output SPW,
  output SPINC,
  output SPDEC,
  output LHR,
  output LHW,
  output LLR,
  output LLW,
  output MALW,
  output MAHW,
  output INTACK,
  output HLT,
  output TRR,
  output MR,
  output MW,
  output TW,
  output MAINC,
  output MADEC,
  output I_0,
  output I_1,
  output I_2,
  output I_3,
  output I_4,
  output I_5,
  output I_6,
  output I_7
);

  wire and_1_out, demultiplexer_1_out_9, demultiplexer_1_out_10, demultiplexer_1_out_11,
       demultiplexer_1_out_12, demultiplexer_1_out_13, demultiplexer_1_out_14, demultiplexer_1_out_15,
       flagregister_1_o0, flagsregister4b_1_o0, flagsregister4b_1_o1, flagsregister4b_1_o2,
       flagsregister4b_1_o3, interrupthandler_1_blkinst, lookuptable_1_out, not_1_out, not_2_out, not_3_out,
       or_1_out, or_2_out, or_3_out, or_4_out, or_5_out, or_6_out, or_7_out, or_8_out, or_9_out, reset_1_out,
       xor_1_out, xor_2_out;
  wire [4:0] counter_1_out;
  wire [61:2] interrupthandler_1_inst;

  or or_1 (or_1_out, ~reset_1_out, CLK);  // Or
  or or_2 (or_2_out, or_8_out, ~reset_1_out);  // Or
  Reset reset_1 (.out(reset_1_out));
  or or_3 (or_3_out, I0, FC);
  or or_4 (or_4_out, I1, FN);
  or or_5 (or_5_out, I2, F0);
  or or_6 (or_6_out, I3, FO);
  Counter #(.Bits(5)) counter_1 (.en(1'b1), .C(not_1_out), .clr(or_2_out), .out(counter_1_out));  // open: ovf
  not not_1 (not_1_out, or_1_out);
  not not_2 (not_2_out, or_1_out);
  Register I (
    .CLK(or_1_out), .E(1'b1), .R(1'b1), .W(interrupthandler_1_inst[35]), .D0(I0), .D1(I1), .D2(I2), .D3(I3),
    .D4(I4), .D5(I5), .D6(I6), .D7(I7), .O0(I_0), .O1(I_1), .O2(I_2), .O3(I_3), .O4(I_4), .O5(I_5), .O6(I_6),
    .O7(I_7));
  FlagsRegister4b flagsregister4b_1 (
    .CLK(not_2_out), .F0(or_3_out), .S0(interrupthandler_1_inst[39]), .R0(interrupthandler_1_inst[38]),
    .E0(interrupthandler_1_inst[40]), .F1(or_4_out), .S1(1'b0), .R1(1'b0), .E1(interrupthandler_1_inst[42]),
    .F2(or_5_out), .S2(1'b0), .R2(1'b0), .E2(interrupthandler_1_inst[43]), .F3(or_6_out), .S3(1'b0),
    .R3(1'b0), .E3(interrupthandler_1_inst[44]), .O0(flagsregister4b_1_o0), .O1(flagsregister4b_1_o1),
    .O2(flagsregister4b_1_o2), .O3(flagsregister4b_1_o3));
  FlagRegister flagregister_1 (
    .CLK(not_2_out), .F0(I4), .S0(interrupthandler_1_inst[46]), .R0(interrupthandler_1_inst[45]),
    .E0(interrupthandler_1_inst[47]), .O0(flagregister_1_o0));
  InterruptHandler interrupthandler_1 (
    .S0(counter_1_out[0]), .S1(counter_1_out[1]), .S2(counter_1_out[2]), .S3(counter_1_out[3]), .INT(INT),
    .IRQ(or_7_out), .IMF(flagregister_1_o0), .INTACK(INTACK), .BLKINST(interrupthandler_1_blkinst),
    .INST({interrupthandler_1_inst[61], MAINC, interrupthandler_1_inst[59], TW, interrupthandler_1_inst[57:54], TRR, interrupthandler_1_inst[52], HLT, INTACK, interrupthandler_1_inst[49:38], MW, MR, interrupthandler_1_inst[35], MAHW, MALW, LLW, LLR, LHW, LHR, SPDEC, SPINC, SPW, SPR, PCLW, PCLR, PCHW, PCHR, PCE, ZW, ZR, YW, YR, XW, XR, AW, AR, interrupthandler_1_inst[11:8], MADEC, interrupthandler_1_inst[6:2], ALU_B, ALUE}),
    .D0(D0), .D1(D1), .D2(D2), .D3(D3), .D4(D4), .D5(D5), .D6(D6), .D7(D7));
  or or_7 (or_7_out, interrupthandler_1_inst[49], IRQ);
  not not_3 (not_3_out, interrupthandler_1_blkinst);
  PinControl8b pincontrol8b_1 (
    .E(interrupthandler_1_inst[48]), .D0(flagsregister4b_1_o3), .D1(flagsregister4b_1_o2),
    .D2(flagsregister4b_1_o1), .D3(flagsregister4b_1_o0), .D4(flagregister_1_o0), .D5(1'b0), .D6(1'b0),
    .D7(1'b0), .O0(D0), .O1(D1), .O2(D2), .O3(D3), .O4(D4), .O5(D5), .O6(D6), .O7(D7));
  ROM #(.AddrBits(13), .Bits(62)) rom_1 (
    .A({I_0, I_1, I_2, I_3, I_4, I_5, I_6, I_7, counter_1_out}), .sel(not_3_out),
    .D({interrupthandler_1_inst[61], MAINC, interrupthandler_1_inst[59], TW, interrupthandler_1_inst[57:54], TRR, interrupthandler_1_inst[52], HLT, INTACK, interrupthandler_1_inst[49:38], MW, MR, interrupthandler_1_inst[35], MAHW, MALW, LLW, LLR, LHW, LHR, SPDEC, SPINC, SPW, SPR, PCLW, PCLR, PCHW, PCHR, PCE, ZW, ZR, YW, YR, XW, XR, AW, AR, interrupthandler_1_inst[11:8], MADEC, interrupthandler_1_inst[6:2], ALU_B, ALUE}));
  PinControl8b pincontrol8b_2 (
    .E(interrupthandler_1_inst[59]), .D0(1'b0), .D1(1'b0), .D2(1'b0), .D3(1'b0), .D4(1'b0), .D5(1'b0),
    .D6(1'b0), .D7(interrupthandler_1_inst[41]), .O0(D0), .O1(D1), .O2(D2), .O3(D3), .O4(D4), .O5(D5),
    .O6(D6), .O7(D7));
  LookUpTable lookuptable_1 (
    .in0(interrupthandler_1_inst[55]), .in1(interrupthandler_1_inst[56]), .in2(flagsregister4b_1_o0),
    .in3(flagsregister4b_1_o1), .in4(flagsregister4b_1_o2), .in5(flagsregister4b_1_o3),
    .out(lookuptable_1_out));
  xor xor_1 (xor_1_out, interrupthandler_1_inst[54], lookuptable_1_out);
  and and_1 (and_1_out, xor_1_out, interrupthandler_1_inst[57]);
  LED led_1 (.in(interrupthandler_1_inst[8]));
  LED led_2 (.in(interrupthandler_1_inst[9]));
  LED led_3 (.in(interrupthandler_1_inst[10]));
  LED led_4 (.in(interrupthandler_1_inst[11]));
  or or_8 (or_8_out, interrupthandler_1_inst[52], and_1_out);
  xor xor_2 (xor_2_out, flagsregister4b_1_o0, interrupthandler_1_inst[61]);
  assign ALUC = ~interrupthandler_1_inst[41] ? interrupthandler_1_inst[2] : 1'bz;  // DriverInvSel driverinvsel_1
  assign ALUC = interrupthandler_1_inst[41] ? xor_2_out : 1'bz;  // Driver driver_1
  or or_9 (or_9_out, interrupthandler_1_inst[3], interrupthandler_1_inst[4], interrupthandler_1_inst[5], interrupthandler_1_inst[6]);
  Demultiplexer #(.Selector_Bits(4)) demultiplexer_1 (
    .sel(interrupthandler_1_inst[6:3]), .in(or_9_out), .out_0(ALUADD), .out_1(ALUAND), .out_2(ALUOR),
    .out_3(ALUNOT), .out_4(ALUXOR), .out_5(ALUSL), .out_6(ALUSR), .out_7(ALURL), .out_8(ALURR),
    .out_9(demultiplexer_1_out_9), .out_10(demultiplexer_1_out_10), .out_11(demultiplexer_1_out_11),
    .out_12(demultiplexer_1_out_12), .out_13(demultiplexer_1_out_13), .out_14(demultiplexer_1_out_14),
    .out_15(demultiplexer_1_out_15));
  LED led_5 (.in(demultiplexer_1_out_9));
  LED led_6 (.in(demultiplexer_1_out_10));
  LED led_7 (.in(demultiplexer_1_out_11));
  LED led_8 (.in(demultiplexer_1_out_12));
  LED led_9 (.in(demultiplexer_1_out_13));
  LED led_10 (.in(demultiplexer_1_out_14));
  LED led_11 (.in(demultiplexer_1_out_15));

  // Other names for the same wires on the sheet: I0_t = I_0; I1_t = I_1; I2_t = I_2; I3_t = I_3; I4_t = I_4;
  //   I5_t = I_5; I6_t = I_6; I7_t = I_7

  // Notes on the sheet:
  //   IW
  //   IMF E/S/R
  //   VF E
  //   ZF E
  //   NF E
  //   CF E/S/R
  //   SCF
  //   CCF
  //   ECF
  //   ENF
  //   EZF
  //   EVF
  //   SIMF
  //   CIMF
  //   EIMF
  //   FTB
  //   CC
  //   contents of rom_1 (hex, n*v repeats v):
  //   200800000,400200000,1000001800100000,10000000000000,28*0,200800000
  //   ,400200000,1000001800100000,1000001000180000,1200100000,400040000
  //   ,10001000002000,25*0,200800000,400200000,1000001800100000,1200100000
  //   ,800000400000000,10001000002000,26*0,200800000,400200000,1000001800100000
  //   ,10001000102000,28*0,200800000,400200000,1000001800100000,1000001000180000
  //   ,1200100000,400040000,10001000008000,25*0,200800000,400200000
  //   ,1000001800100000,1200100000,800000400000000,10001000008000,26*0
  //   ,200800000,400200000,1000001800100000,10001000108000,28*0,200800000
  //   ,400200000,1000001800100000,1000001000180000,1200100000,400040000
  //   ,10001000020000,25*0,200800000,400200000,1000001800100000,1200100000
  //   ,800000400000000,10001000020000,26*0,200800000,400200000,1000001800100000
  //   ,10001000120000,28*0,200800000,400200000,1000001800100000,1000001000180000
  //   ,1200100000,400040000,1000001040000000,10001100000000,24*0,200800000
  //   ,400200000,1000001800100000,1200100000,800000400000000,1000001040000000
  //   ,10001100000000,25*0,200800000,400200000,1000001800100000,1000001040100000
  //   ,10001100100000,27*0,200800000,400200000,1000001800100000,1000001000180000
  //   ,1200100000,400040000,10001100000000,25*0,200800000,400200000
  //   ,1000001800100000,1200100000,800000400000000,10001100000000,26*0
  //   ,200800000,400200000,1000001800100000,10001100100000,28*0,200800000
  //   ,400200000,1000001800100000,1000001000180000,1200100000,400040000
  //   ,10001040000000,25*0,200800000,400200000,1000001800100000,1200100000
  //   ,800000400000000,10001040000000,26*0,200800000,400200000,1000001800100000
  //   ,10001040100000,28*0,200800000,400200000,1000001800100000,810000000002000
  //   ,28*0,200800000,400200000,1000001800100000,810000000008000,28*0
  //   ,200800000,400200000,1000001800100000,810000000020000,28*0,200800000
  //   ,400200000,1000001800100000,800000100000000,810000040000000,27*0
  //   ,200800000,400200000,1000001800100000,810000100000000,28*0,200800000
  //   ,400200000,1000001800100000,810000040000000,28*0,200800000,400200000
  //   ,1000001800100000,1000001000180000,1200100000,400040000,10002000001000
  //   ,25*0,200800000,400200000,1000001800100000,1200100000,800000400000000
  //   ,10002000001000,26*0,200800000,400200000,1000001800100000,1000001000180000
  //   ,1200100000,400040000,10002000004000,25*0,200800000,400200000
  //   ,1000001800100000,1200100000,800000400000000,10002000004000,26*0
  //   ,200800000,400200000,1000001800100000,1000001000180000,1200100000
  //   ,400040000,10002000010000,25*0,200800000,400200000,1000001800100000
  //   ,1200100000,800000400000000,10002000010000,26*0,200800000,400200000
  //   ,1000001800100000,1000001000180000,1200100000,400040000,1000002020000000
  //   ,10001080000000,24*0,200800000,400200000,1000001800100000,1200100000
  //   ,800000400000000,1000002020000000,10002080000000,25*0,200800000
  //   ,400200000,1000001800100000,1000001000180000,1200100000,400040000
  //   ,10002080000000,25*0,200800000,400200000,1000001800100000,1200100000
  //   ,800000400000000,10002080000000,26*0,200800000,400200000,1000001800100000
  //   ,1000001000180000,1200100000,400040000,10002020000000,25*0,200800000
  //   ,400200000,1000001800100000,1200100000,800000400000000,10002020000000
  //   ,26*0,200800000,400200000,1000001800100000,1000001000180000,1200100000
  //   ,400040000,810002000000000,25*0,200800000,400200000,1000001800100000
  //   ,1200100000,800000400000000,810002000000000,26*0,200800000,400200000
  //   ,1000001800100000,10000000009000,28*0,200800000,400200000,1000001800100000
  //   ,10000000006000,28*0,200800000,400200000,1000001800100000,10000000021000
  //   ,28*0,200800000,400200000,1000001800100000,10000000012000,28*0
  //   ,200800000,400200000,1000001800100000,10000100001000,28*0,200800000
  //   ,400200000,1000001800100000,10000080002000,28*0,200800000,400200000
  //   ,1000001800100000,10000040001000,28*0,200800000,400200000,1000001800100000
  //   ,10000020002000,28*0,200800000,400200000,1000001800100000,10000004001000
  //   ,28*0,200800000,400200000,1000001800100000,10000002002000,28*0
  //   ,200800000,400200000,1000001800100000,10000000024000,28*0,200800000
  //   ,400200000,1000001800100000,10000000018000,28*0,200800000,400200000
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  //   ALU
  //   Reg
  //   MEM
  //   F/INT
  //   MISC
  //   contents of lookuptable_1 (hex, n*v repeats v):
  //   a,0,0,0,1,0,0,0,a,1,a,0,1,1,4*0,1,0,1,0,1,0,0,1,1,0,1,1,1,0,0
  //   ,a,0,1,1,0,0,1,0,1,0,1,1,1,0,1,0,0,1,1,1,0,1,1,0,7*1
  //   IRQ
  //   SCF
  //   CCF
  //   ECF
  //   OCF
  //   ENF
  //   EZF
  //   EVF
  //   SIMF
  //   CIMF
  //   EIMF
endmodule
