// Digital circuit Interrupt Sequencer.dig as structural Verilog
module Interrupt_Sequencer (
  input  INTACKI,
  input  I0,
  input  I1,
  input  I2,
  input  I3,
  input  I4,
  input  I5,
  input  I6,
  input  I7,
  output INT0,
  output INT1,
  output INT2,
  output INT3,
  output INT4,
  output INT5,
  output INT6,
  output INT7,
  output INTACKO,
  output IRQ
);

  wire and_1_out, and_3_out, and_5_out, and_7_out, and_9_out, and_11_out, and_13_out, not_1_out, not_2_out,
       not_3_out, not_4_out, not_5_out, not_6_out, not_7_out, not_8_out, rising_edge_detector_1_out,
       rs_ff_as_1_q, rs_ff_as_2_q, rs_ff_as_3_q, rs_ff_as_4_q, rs_ff_as_5_q, rs_ff_as_6_q, rs_ff_as_7_q,
       rs_ff_as_8_q;

  Rising_Edge_Detector rising_edge_detector_1 (.CLK(INTACKI), .OUT(rising_edge_detector_1_out));
  and and_1 (and_1_out, rising_edge_detector_1_out, not_1_out);
  RS_FF_AS rs_ff_as_1 (.S(I0), .R(INT0), .Q(rs_ff_as_1_q));  // open: nQ
  not not_1 (not_1_out, rs_ff_as_1_q);
  and and_2 (INT0, rs_ff_as_1_q, rising_edge_detector_1_out);
  and and_3 (and_3_out, and_1_out, not_2_out);
  RS_FF_AS rs_ff_as_2 (.S(I1), .R(INT1), .Q(rs_ff_as_2_q));  // open: nQ
  not not_2 (not_2_out, rs_ff_as_2_q);
  and and_4 (INT1, rs_ff_as_2_q, and_1_out);
  and and_5 (and_5_out, and_3_out, not_3_out);
  RS_FF_AS rs_ff_as_3 (.S(I2), .R(INT2), .Q(rs_ff_as_3_q));  // open: nQ
  not not_3 (not_3_out, rs_ff_as_3_q);
  and and_6 (INT2, rs_ff_as_3_q, and_3_out);
  and and_7 (and_7_out, and_5_out, not_4_out);
  RS_FF_AS rs_ff_as_4 (.S(I3), .R(INT3), .Q(rs_ff_as_4_q));  // open: nQ
  not not_4 (not_4_out, rs_ff_as_4_q);
  and and_8 (INT3, rs_ff_as_4_q, and_5_out);
  and and_9 (and_9_out, and_7_out, not_5_out);
  RS_FF_AS rs_ff_as_5 (.S(I4), .R(INT4), .Q(rs_ff_as_5_q));  // open: nQ
  not not_5 (not_5_out, rs_ff_as_5_q);
  and and_10 (INT4, rs_ff_as_5_q, and_7_out);
  and and_11 (and_11_out, and_9_out, not_6_out);
  RS_FF_AS rs_ff_as_6 (.S(I5), .R(INT5), .Q(rs_ff_as_6_q));  // open: nQ
  not not_6 (not_6_out, rs_ff_as_6_q);
  and and_12 (INT5, rs_ff_as_6_q, and_9_out);
  and and_13 (and_13_out, and_11_out, not_7_out);
  RS_FF_AS rs_ff_as_7 (.S(I6), .R(INT6), .Q(rs_ff_as_7_q));  // open: nQ
  not not_7 (not_7_out, rs_ff_as_7_q);
  and and_14 (INT6, rs_ff_as_7_q, and_11_out);
  and and_15 (INTACKO, and_13_out, not_8_out);
  RS_FF_AS rs_ff_as_8 (.S(I7), .R(INT7), .Q(rs_ff_as_8_q));  // open: nQ
  not not_8 (not_8_out, rs_ff_as_8_q);
  and and_16 (INT7, rs_ff_as_8_q, and_13_out);
  or or_1 (IRQ, rs_ff_as_8_q, rs_ff_as_7_q, rs_ff_as_6_q, rs_ff_as_5_q, rs_ff_as_4_q, rs_ff_as_3_q, rs_ff_as_2_q, rs_ff_as_1_q);
endmodule
