// Digital circuit InterruptHandler.dig as structural Verilog
module InterruptHandler (
  input  S0,
  input  S1,
  input  S2,
  input  S3,
  input  INT,
  input  IRQ,
  input  IMF,
  input  INTACK,
  output BLKINST,
  output [61:0] INST,
  output D0,
  output D1,
  output D2,
  output D3,
  output D4,
  output D5,
  output D6,
  output D7
);

  wire and_1_out, and_2_out, and_3_out, and_4_out, and_5_out, and_6_out, or_1_out, or_2_out, reset_1_out;
  wire [63:0] rom_1_d;

  and and_1 (and_1_out, IRQ, ~IMF);  // And
  or or_1 (or_1_out, INT, and_1_out);
  and and_2 (and_2_out, ~INT, and_1_out);  // And
  and and_3 (and_3_out, ~S0, ~S1, ~S2, ~S3);  // And
  and and_4 (and_4_out, and_3_out, or_1_out);
  or or_2 (or_2_out, INTACK, reset_1_out);
  Reset #(.invertOutput("false")) reset_1 (.out(reset_1_out));
  RS_FF_AS rs_ff_as_1 (.S(and_4_out), .R(or_2_out), .Q(BLKINST));  // open: nQ
  ROM #(.AddrBits(4), .Bits(64)) rom_1 (.A({S3, S2, S1, S0}), .sel(BLKINST), .D(rom_1_d));
  assign rom_1_d = ~BLKINST ? {64{1'b0}} : 64'bz;  // DriverInvSel driverinvsel_1
  and and_5 (and_5_out, rom_1_d[63], INT);
  and and_6 (and_6_out, rom_1_d[63], and_2_out);
  assign INST = BLKINST ? rom_1_d[61:0] : 62'bz;  // Driver driver_1
  PinControl8b pincontrol8b_1 (
    .E(rom_1_d[62]), .D0(1'b1), .D1(1'b1), .D2(1'b1), .D3(1'b1), .D4(1'b1), .D5(1'b1), .D6(1'b1), .D7(1'b1),
    .O0(D0), .O1(D1), .O2(D2), .O3(D3), .O4(D4), .O5(D5), .O6(D6), .O7(D7));
  PinControl8b pincontrol8b_2 (
    .E(and_5_out), .D0(1'b1), .D1(1'b1), .D2(1'b1), .D3(1'b1), .D4(1'b1), .D5(1'b1), .D6(1'b1), .D7(1'b0),
    .O0(D0), .O1(D1), .O2(D2), .O3(D3), .O4(D4), .O5(D5), .O6(D6), .O7(D7));
  PinControl8b pincontrol8b_3 (
    .E(and_6_out), .D0(1'b1), .D1(1'b1), .D2(1'b1), .D3(1'b1), .D4(1'b1), .D5(1'b1), .D6(1'b0), .D7(1'b0),
    .O0(D0), .O1(D1), .O2(D2), .O3(D3), .O4(D4), .O5(D5), .O6(D6), .O7(D7));

  // Notes on the sheet:
  //   contents of rom_1 (hex, n*v repeats v):
  //   800020400000000,20a000000,1000002008200000,1000002008800000,1002000000000,4000000400000000,
  //   8000000200000000,1000001000400000,14001001000000
endmodule
