// Digital circuit FlagRegister.dig as structural Verilog
module FlagRegister (
  input  CLK,
  input  F0,
  input  S0,
  input  R0,
  input  E0,
  output O0
);

  wire and_1_out, and_2_out, not_1_out, or_1_out;

  or or_1 (or_1_out, F0, S0);
  not not_1 (not_1_out, R0);
  and and_1 (and_1_out, or_1_out, not_1_out);
  and and_2 (and_2_out, CLK, E0);
  D_FF d_ff_1 (.D(and_1_out), .C(and_2_out), .Q(O0));  // open: nQ
endmodule
