// Digital circuit FlagsRegister4b.dig as structural Verilog
module FlagsRegister4b (
  input  CLK,
  input  F0,
  input  S0,
  input  R0,
  input  E0,
  input  F1,
  input  S1,
  input  R1,
  input  E1,
  input  F2,
  input  S2,
  input  R2,
  input  E2,
  input  F3,
  input  S3,
  input  R3,
  input  E3,
  output O0,
  output O1,
  output O2,
  output O3
);

  wire and_1_out, and_2_out, and_3_out, and_4_out, and_5_out, and_6_out, and_7_out, and_8_out, not_1_out,
       not_2_out, not_3_out, not_4_out, or_1_out, or_2_out, or_3_out, or_4_out;

  or or_1 (or_1_out, F0, S0);
  not not_1 (not_1_out, R0);
  or or_2 (or_2_out, F1, S1);
  not not_2 (not_2_out, R1);
  or or_3 (or_3_out, F2, S2);
  not not_3 (not_3_out, R2);
  or or_4 (or_4_out, F3, S3);
  not not_4 (not_4_out, R3);
  and and_1 (and_1_out, or_1_out, not_1_out);
  and and_2 (and_2_out, or_2_out, not_2_out);
  and and_3 (and_3_out, or_3_out, not_3_out);
  and and_4 (and_4_out, or_4_out, not_4_out);
  and and_5 (and_5_out, CLK, E0);
  and and_6 (and_6_out, CLK, E1);
  and and_7 (and_7_out, CLK, E2);
  and and_8 (and_8_out, CLK, E3);
  D_FF d_ff_1 (.D(and_1_out), .C(and_5_out), .Q(O0));  // open: nQ
  D_FF d_ff_2 (.D(and_2_out), .C(and_6_out), .Q(O1));  // open: nQ
  D_FF d_ff_3 (.D(and_3_out), .C(and_7_out), .Q(O2));  // open: nQ
  D_FF d_ff_4 (.D(and_4_out), .C(and_8_out), .Q(O3));  // open: nQ
endmodule
