// Digital circuit MAReg16++.dig as structural Verilog
module MAReg16 (
  input  CLK,
  input  INC,
  input  DEC,
  input  WL,
  input  WH,
  input  D0,
  input  D1,
  input  D2,
  input  D3,
  input  D4,
  input  D5,
  input  D6,
  input  D7,
  output O0,
  output O1,
  output O2,
  output O3,
  output O4,
  output O5,
  output O6,
  output O7,
  output O8,
  output O9,
  output O10,
  output O11,
  output O12,
  output O13,
  output O14,
  output O15
);

  wire incrementer8b_2_co, or_1_out, or_2_out, pincontrol8b_1_o0, pincontrol8b_1_o1, pincontrol8b_1_o2,
       pincontrol8b_1_o3, pincontrol8b_1_o4, pincontrol8b_1_o5, pincontrol8b_1_o6, pincontrol8b_1_o7,
       pincontrol8b_2_o0, pincontrol8b_2_o1, pincontrol8b_2_o2, pincontrol8b_2_o3, pincontrol8b_2_o4,
       pincontrol8b_2_o5, pincontrol8b_2_o6, pincontrol8b_2_o7;

  PinControl8b pincontrol8b_1 (
    .E(WH), .D0(D0), .D1(D1), .D2(D2), .D3(D3), .D4(D4), .D5(D5), .D6(D6), .D7(D7), .O0(pincontrol8b_1_o0),
    .O1(pincontrol8b_1_o1), .O2(pincontrol8b_1_o2), .O3(pincontrol8b_1_o3), .O4(pincontrol8b_1_o4),
    .O5(pincontrol8b_1_o5), .O6(pincontrol8b_1_o6), .O7(pincontrol8b_1_o7));
  PinControl8b pincontrol8b_2 (
    .E(WL), .D0(D0), .D1(D1), .D2(D2), .D3(D3), .D4(D4), .D5(D5), .D6(D6), .D7(D7), .O0(pincontrol8b_2_o0),
    .O1(pincontrol8b_2_o1), .O2(pincontrol8b_2_o2), .O3(pincontrol8b_2_o3), .O4(pincontrol8b_2_o4),
    .O5(pincontrol8b_2_o5), .O6(pincontrol8b_2_o6), .O7(pincontrol8b_2_o7));
  or or_1 (or_1_out, WH, DEC, INC);
  or or_2 (or_2_out, WL, DEC, INC);
  Register register_1 (
    .CLK(CLK), .E(1'b1), .R(1'b1), .W(or_1_out), .D0(pincontrol8b_1_o0), .D1(pincontrol8b_1_o1),
    .D2(pincontrol8b_1_o2), .D3(pincontrol8b_1_o3), .D4(pincontrol8b_1_o4), .D5(pincontrol8b_1_o5),
    .D6(pincontrol8b_1_o6), .D7(pincontrol8b_1_o7), .O0(O0), .O1(O1), .O2(O2), .O3(O3), .O4(O4), .O5(O5),
    .O6(O6), .O7(O7));
  Register register_2 (
    .CLK(CLK), .E(1'b1), .R(1'b1), .W(or_2_out), .D0(pincontrol8b_2_o0), .D1(pincontrol8b_2_o1),
    .D2(pincontrol8b_2_o2), .D3(pincontrol8b_2_o3), .D4(pincontrol8b_2_o4), .D5(pincontrol8b_2_o5),
    .D6(pincontrol8b_2_o6), .D7(pincontrol8b_2_o7), .O0(O8), .O1(O9), .O2(O10), .O3(O11), .O4(O12), .O5(O13),
    .O6(O14), .O7(O15));
  Incrementer8b incrementer8b_1 (
    .E(INC), .D0(O0), .D1(O1), .D2(O2), .D3(O3), .D4(O4), .D5(O5), .D6(O6), .D7(O7),
    .INC(incrementer8b_2_co), .O0(pincontrol8b_1_o0), .O1(pincontrol8b_1_o1), .O2(pincontrol8b_1_o2),
    .O3(pincontrol8b_1_o3), .O4(pincontrol8b_1_o4), .O5(pincontrol8b_1_o5), .O6(pincontrol8b_1_o6),
    .O7(pincontrol8b_1_o7));  // open: CO
  Incrementer8b incrementer8b_2 (
    .E(INC), .D0(O8), .D1(O9), .D2(O10), .D3(O11), .D4(O12), .D5(O13), .D6(O14), .D7(O15), .INC(INC),
    .O0(pincontrol8b_2_o0), .O1(pincontrol8b_2_o1), .O2(pincontrol8b_2_o2), .O3(pincontrol8b_2_o3),
    .O4(pincontrol8b_2_o4), .O5(pincontrol8b_2_o5), .O6(pincontrol8b_2_o6), .O7(pincontrol8b_2_o7),
    .CO(incrementer8b_2_co));
  Decrementer16b decrementer16b_1 (
    .E(DEC), .D0(O0), .D1(O1), .D2(O2), .D3(O3), .D4(O4), .D5(O5), .D6(O6), .D7(O7), .D8(O8), .D9(O9),
    .D10(O10), .D11(O11), .D12(O12), .D13(O13), .D14(O14), .D15(O15), .DEC(DEC), .O0(pincontrol8b_1_o0),
    .O1(pincontrol8b_1_o1), .O2(pincontrol8b_1_o2), .O3(pincontrol8b_1_o3), .O4(pincontrol8b_1_o4),
    .O5(pincontrol8b_1_o5), .O6(pincontrol8b_1_o6), .O7(pincontrol8b_1_o7), .O8(pincontrol8b_2_o0),
    .O9(pincontrol8b_2_o1), .O10(pincontrol8b_2_o2), .O11(pincontrol8b_2_o3), .O12(pincontrol8b_2_o4),
    .O13(pincontrol8b_2_o5), .O14(pincontrol8b_2_o6), .O15(pincontrol8b_2_o7));  // open: CO
endmodule
