// Digital circuit MAReg16b.dig as structural Verilog
module MAReg16b (
  input  CLK,
  input  E,
  input  WL,
  input  WH,
  input  D0,
  input  D1,
  input  D2,
  input  D3,
  input  D4,
  input  D5,
  input  D6,
  input  D7,
  output O0,
  output O1,
  output O2,
  output O3,
  output O4,
  output O5,
  output O6,
  output O7,
  output O8,
  output O9,
  output O10,
  output O11,
  output O12,
  output O13,
  output O14,
  output O15
);

  wire and_1_out, and_2_out, and_3_out, rising_edge_detector_1_out;

  Rising_Edge_Detector rising_edge_detector_1 (.CLK(CLK), .OUT(rising_edge_detector_1_out));
  and and_1 (and_1_out, rising_edge_detector_1_out, E);
  and and_2 (and_2_out, WL, and_1_out);
  and and_3 (and_3_out, WH, and_1_out);
  D_FF d_ff_1 (.D(D0), .C(and_2_out), .Q(O0));  // open: nQ
  D_FF d_ff_2 (.D(D1), .C(and_2_out), .Q(O1));  // open: nQ
  D_FF d_ff_3 (.D(D2), .C(and_2_out), .Q(O2));  // open: nQ
  D_FF d_ff_4 (.D(D3), .C(and_2_out), .Q(O3));  // open: nQ
  D_FF d_ff_5 (.D(D4), .C(and_2_out), .Q(O4));  // open: nQ
  D_FF d_ff_6 (.D(D5), .C(and_2_out), .Q(O5));  // open: nQ
  D_FF d_ff_7 (.D(D6), .C(and_2_out), .Q(O6));  // open: nQ
  D_FF d_ff_8 (.D(D7), .C(and_2_out), .Q(O7));  // open: nQ
  D_FF d_ff_9 (.D(D0), .C(and_3_out), .Q(O8));  // open: nQ
  D_FF d_ff_10 (.D(D1), .C(and_3_out), .Q(O9));  // open: nQ
  D_FF d_ff_11 (.D(D2), .C(and_3_out), .Q(O10));  // open: nQ
  D_FF d_ff_12 (.D(D3), .C(and_3_out), .Q(O11));  // open: nQ
  D_FF d_ff_13 (.D(D4), .C(and_3_out), .Q(O12));  // open: nQ
  D_FF d_ff_14 (.D(D5), .C(and_3_out), .Q(O13));  // open: nQ
  D_FF d_ff_15 (.D(D6), .C(and_3_out), .Q(O14));  // open: nQ
  D_FF d_ff_16 (.D(D7), .C(and_3_out), .Q(O15));  // open: nQ
endmodule
