// Digital circuit PCH.dig as structural Verilog
module PCH (
  input  CLK,
  input  E,
  input  R,
  input  W,
  input  D0,
  input  D1,
  input  D2,
  input  D3,
  input  D4,
  input  D5,
  input  D6,
  input  D7,
  output O0,
  output O1,
  output O2,
  output O3,
  output O4,
  output O5,
  output O6,
  output O7
);

  wire and_1_out, and_2_out, and_3_out, d_ff_1_q, d_ff_2_q, d_ff_3_q, d_ff_4_q, d_ff_5_q, d_ff_6_q, d_ff_7_q,
       d_ff_8_q, rising_edge_detector_1_out;

  Rising_Edge_Detector rising_edge_detector_1 (.CLK(CLK), .OUT(rising_edge_detector_1_out));
  and and_1 (and_1_out, rising_edge_detector_1_out, E);
  and and_2 (and_2_out, E, R);
  and and_3 (and_3_out, W, and_1_out);
  D_FF d_ff_1 (.D(D0), .C(and_3_out), .Q(d_ff_1_q));  // open: nQ
  D_FF d_ff_2 (.D(D1), .C(and_3_out), .Q(d_ff_2_q));  // open: nQ
  D_FF d_ff_3 (.D(D2), .C(and_3_out), .Q(d_ff_3_q));  // open: nQ
  D_FF d_ff_4 (.D(D3), .C(and_3_out), .Q(d_ff_4_q));  // open: nQ
  D_FF d_ff_5 (.D(D4), .C(and_3_out), .Q(d_ff_5_q));  // open: nQ
  D_FF d_ff_6 (.D(D5), .C(and_3_out), .Q(d_ff_6_q));  // open: nQ
  D_FF #(.Default(1)) d_ff_7 (.D(D6), .C(and_3_out), .Q(d_ff_7_q));  // open: nQ
  D_FF d_ff_8 (.D(D7), .C(and_3_out), .Q(d_ff_8_q));  // open: nQ
  assign O0 = and_2_out ? d_ff_1_q : 1'bz;  // Driver driver_1
  assign O1 = and_2_out ? d_ff_2_q : 1'bz;  // Driver driver_2
  assign O2 = and_2_out ? d_ff_3_q : 1'bz;  // Driver driver_3
  assign O3 = and_2_out ? d_ff_4_q : 1'bz;  // Driver driver_4
  assign O4 = and_2_out ? d_ff_5_q : 1'bz;  // Driver driver_5
  assign O5 = and_2_out ? d_ff_6_q : 1'bz;  // Driver driver_6
  assign O6 = and_2_out ? d_ff_7_q : 1'bz;  // Driver driver_7
  assign O7 = and_2_out ? d_ff_8_q : 1'bz;  // Driver driver_8
endmodule
