// Digital circuit Reg16.dig as structural Verilog
module Reg16 (
  input  CLK,
  input  E,
  input  R,
  input  W,
  input  D0,
  input  D1,
  input  D2,
  input  D3,
  input  D4,
  input  D5,
  input  D6,
  input  D7,
  input  D8,
  input  D9,
  input  D10,
  input  D11,
  input  D12,
  input  D13,
  input  D14,
  input  D15,
  output O0,
  output O1,
  output O2,
  output O3,
  output O4,
  output O5,
  output O6,
  output O7,
  output O8,
  output O9,
  output O10,
  output O11,
  output O12,
  output O13,
  output O14,
  output O15
);

  wire and_1_out, and_2_out, and_3_out, d_ff_1_q, d_ff_2_q, d_ff_3_q, d_ff_4_q, d_ff_5_q, d_ff_6_q, d_ff_7_q,
       d_ff_8_q, d_ff_9_q, d_ff_10_q, d_ff_11_q, d_ff_12_q, d_ff_13_q, d_ff_14_q, d_ff_15_q, d_ff_16_q,
       rising_edge_detector_1_out;

  Rising_Edge_Detector rising_edge_detector_1 (.CLK(CLK), .OUT(rising_edge_detector_1_out));
  and and_1 (and_1_out, rising_edge_detector_1_out, E);
  and and_2 (and_2_out, E, R);
  and and_3 (and_3_out, W, and_1_out);
  D_FF d_ff_1 (.D(D0), .C(and_3_out), .Q(d_ff_1_q));  // open: nQ
  D_FF d_ff_2 (.D(D1), .C(and_3_out), .Q(d_ff_2_q));  // open: nQ
  D_FF d_ff_3 (.D(D2), .C(and_3_out), .Q(d_ff_3_q));  // open: nQ
  D_FF d_ff_4 (.D(D3), .C(and_3_out), .Q(d_ff_4_q));  // open: nQ
  D_FF d_ff_5 (.D(D4), .C(and_3_out), .Q(d_ff_5_q));  // open: nQ
  D_FF d_ff_6 (.D(D5), .C(and_3_out), .Q(d_ff_6_q));  // open: nQ
  D_FF d_ff_7 (.D(D6), .C(and_3_out), .Q(d_ff_7_q));  // open: nQ
  D_FF d_ff_8 (.D(D7), .C(and_3_out), .Q(d_ff_8_q));  // open: nQ
  D_FF d_ff_9 (.D(D8), .C(and_3_out), .Q(d_ff_9_q));  // open: nQ
  D_FF d_ff_10 (.D(D9), .C(and_3_out), .Q(d_ff_10_q));  // open: nQ
  D_FF d_ff_11 (.D(D10), .C(and_3_out), .Q(d_ff_11_q));  // open: nQ
  D_FF d_ff_12 (.D(D11), .C(and_3_out), .Q(d_ff_12_q));  // open: nQ
  D_FF d_ff_13 (.D(D12), .C(and_3_out), .Q(d_ff_13_q));  // open: nQ
  D_FF d_ff_14 (.D(D13), .C(and_3_out), .Q(d_ff_14_q));  // open: nQ
  D_FF d_ff_15 (.D(D14), .C(and_3_out), .Q(d_ff_15_q));  // open: nQ
  D_FF d_ff_16 (.D(D15), .C(and_3_out), .Q(d_ff_16_q));  // open: nQ
  assign O0 = and_2_out ? d_ff_1_q : 1'bz;  // Driver driver_1
  assign O1 = and_2_out ? d_ff_2_q : 1'bz;  // Driver driver_2
  assign O2 = and_2_out ? d_ff_3_q : 1'bz;  // Driver driver_3
  assign O3 = and_2_out ? d_ff_4_q : 1'bz;  // Driver driver_4
  assign O4 = and_2_out ? d_ff_5_q : 1'bz;  // Driver driver_5
  assign O5 = and_2_out ? d_ff_6_q : 1'bz;  // Driver driver_6
  assign O6 = and_2_out ? d_ff_7_q : 1'bz;  // Driver driver_7
  assign O7 = and_2_out ? d_ff_8_q : 1'bz;  // Driver driver_8
  assign O8 = and_2_out ? d_ff_9_q : 1'bz;  // Driver driver_9
  assign O9 = and_2_out ? d_ff_10_q : 1'bz;  // Driver driver_10
  assign O10 = and_2_out ? d_ff_11_q : 1'bz;  // Driver driver_11
  assign O11 = and_2_out ? d_ff_12_q : 1'bz;  // Driver driver_12
  assign O12 = and_2_out ? d_ff_13_q : 1'bz;  // Driver driver_13
  assign O13 = and_2_out ? d_ff_14_q : 1'bz;  // Driver driver_14
  assign O14 = and_2_out ? d_ff_15_q : 1'bz;  // Driver driver_15
  assign O15 = and_2_out ? d_ff_16_q : 1'bz;  // Driver driver_16
endmodule
