// Digital circuit StackPointer.dig as structural Verilog
module StackPointer (
  input  CLK,
  input  INC,
  input  DEC,
  input  R,
  input  W,
  input  D0,
  input  D1,
  input  D2,
  input  D3,
  input  D4,
  input  D5,
  input  D6,
  input  D7,
  output O0,
  output O1,
  output O2,
  output O3,
  output O4,
  output O5,
  output O6,
  output O7
);

  wire or_1_out;
  wire [7:0] driver_1_out, register_1_o4, sub_1_s;

  assign driver_1_out[0] = W ? D0 : 1'bz;  // Driver driver_1
  assign driver_1_out[1] = W ? D1 : 1'bz;  // Driver driver_2
  assign driver_1_out[2] = W ? D2 : 1'bz;  // Driver driver_3
  assign driver_1_out[3] = W ? D3 : 1'bz;  // Driver driver_4
  assign driver_1_out[4] = W ? D4 : 1'bz;  // Driver driver_5
  assign driver_1_out[5] = W ? D5 : 1'bz;  // Driver driver_6
  assign driver_1_out[6] = W ? D6 : 1'bz;  // Driver driver_7
  assign driver_1_out[7] = W ? D7 : 1'bz;  // Driver driver_8
  or or_1 (or_1_out, INC, W, DEC);
  Register register_1 (
    .CLK(CLK), .E(1'b1), .R(1'b1), .W(or_1_out), .D0(driver_1_out[0]), .D1(driver_1_out[1]),
    .D2(driver_1_out[2]), .D3(driver_1_out[3]), .D4(driver_1_out[4]), .D5(driver_1_out[5]),
    .D6(driver_1_out[6]), .D7(driver_1_out[7]), .O0(register_1_o4[7]), .O1(register_1_o4[6]),
    .O2(register_1_o4[5]), .O3(register_1_o4[4]), .O4(register_1_o4[3]), .O5(register_1_o4[2]),
    .O6(register_1_o4[1]), .O7(register_1_o4[0]));
  Incrementer8b incrementer8b_1 (
    .E(INC), .D0(register_1_o4[7]), .D1(register_1_o4[6]), .D2(register_1_o4[5]), .D3(register_1_o4[4]),
    .D4(register_1_o4[3]), .D5(register_1_o4[2]), .D6(register_1_o4[1]), .D7(register_1_o4[0]), .INC(INC),
    .O0(driver_1_out[0]), .O1(driver_1_out[1]), .O2(driver_1_out[2]), .O3(driver_1_out[3]),
    .O4(driver_1_out[4]), .O5(driver_1_out[5]), .O6(driver_1_out[6]), .O7(driver_1_out[7]));  // open: CO
  Sub #(.Bits(8)) sub_1 (.a(register_1_o4), .b({8{1'b0}}), .c_i(1'b1), .s(sub_1_s));  // open: c_o
  assign O0 = R ? register_1_o4[7] : 1'bz;  // Driver driver_9
  assign O1 = R ? register_1_o4[6] : 1'bz;  // Driver driver_10
  assign O2 = R ? register_1_o4[5] : 1'bz;  // Driver driver_11
  assign O3 = R ? register_1_o4[4] : 1'bz;  // Driver driver_12
  assign O4 = R ? register_1_o4[3] : 1'bz;  // Driver driver_13
  assign O5 = R ? register_1_o4[2] : 1'bz;  // Driver driver_14
  assign O6 = R ? register_1_o4[1] : 1'bz;  // Driver driver_15
  assign O7 = R ? register_1_o4[0] : 1'bz;  // Driver driver_16
  assign driver_1_out = DEC ? sub_1_s : 8'bz;  // Driver driver_17
endmodule
