// Digital circuit ProgramCounter.dig as structural Verilog
module ProgramCounter (
  input  CLK,
  input  E,
  input  R,
  input  W,
  input  D0,
  input  D1,
  input  D2,
  input  D3,
  input  D4,
  input  D5,
  input  D6,
  input  D7,
  output O0,
  output O1,
  output O2,
  output O3,
  output O4,
  output O5,
  output O6,
  output O7
);

  wire driver_1_out, driver_2_out, driver_3_out, driver_4_out, driver_5_out, driver_6_out, driver_7_out,
       driver_8_out, or_1_out, register_1_o0, register_1_o1, register_1_o2, register_1_o3, register_1_o4,
       register_1_o5, register_1_o6, register_1_o7;

  assign driver_1_out = W ? D0 : 1'bz;  // Driver driver_1
  assign driver_2_out = W ? D1 : 1'bz;  // Driver driver_2
  assign driver_3_out = W ? D2 : 1'bz;  // Driver driver_3
  assign driver_4_out = W ? D3 : 1'bz;  // Driver driver_4
  assign driver_5_out = W ? D4 : 1'bz;  // Driver driver_5
  assign driver_6_out = W ? D5 : 1'bz;  // Driver driver_6
  assign driver_7_out = W ? D6 : 1'bz;  // Driver driver_7
  assign driver_8_out = W ? D7 : 1'bz;  // Driver driver_8
  or or_1 (or_1_out, E, W);
  Register register_1 (
    .CLK(CLK), .E(1'b1), .R(1'b1), .W(or_1_out), .D0(driver_1_out), .D1(driver_2_out), .D2(driver_3_out),
    .D3(driver_4_out), .D4(driver_5_out), .D5(driver_6_out), .D6(driver_7_out), .D7(driver_8_out),
    .O0(register_1_o0), .O1(register_1_o1), .O2(register_1_o2), .O3(register_1_o3), .O4(register_1_o4),
    .O5(register_1_o5), .O6(register_1_o6), .O7(register_1_o7));
  Incrementer8b incrementer8b_1 (
    .E(E), .D0(register_1_o0), .D1(register_1_o1), .D2(register_1_o2), .D3(register_1_o3),
    .D4(register_1_o4), .D5(register_1_o5), .D6(register_1_o6), .D7(register_1_o7), .INC(E),
    .O0(driver_1_out), .O1(driver_2_out), .O2(driver_3_out), .O3(driver_4_out), .O4(driver_5_out),
    .O5(driver_6_out), .O6(driver_7_out), .O7(driver_8_out));  // open: CO
  assign O0 = R ? register_1_o0 : 1'bz;  // Driver driver_9
  assign O1 = R ? register_1_o1 : 1'bz;  // Driver driver_10
  assign O2 = R ? register_1_o2 : 1'bz;  // Driver driver_11
  assign O3 = R ? register_1_o3 : 1'bz;  // Driver driver_12
  assign O4 = R ? register_1_o4 : 1'bz;  // Driver driver_13
  assign O5 = R ? register_1_o5 : 1'bz;  // Driver driver_14
  assign O6 = R ? register_1_o6 : 1'bz;  // Driver driver_15
  assign O7 = R ? register_1_o7 : 1'bz;  // Driver driver_16
endmodule
