// Digital circuit ProgramCounter16.dig as structural Verilog
module ProgramCounter16 (
  input  CLK,
  input  E,
  input  R,
  input  W,
  input  D0,
  input  D1,
  input  D2,
  input  D3,
  input  D4,
  input  D5,
  input  D6,
  input  D7,
  input  D8,
  input  D9,
  input  D10,
  input  D11,
  input  D12,
  input  D13,
  input  D14,
  input  D15,
  output O0,
  output O1,
  output O2,
  output O3,
  output O4,
  output O5,
  output O6,
  output O7,
  output O8,
  output O9,
  output O10,
  output O11,
  output O12,
  output O13,
  output O14,
  output O15
);

  wire driver_1_out, driver_2_out, driver_3_out, driver_4_out, driver_5_out, driver_6_out, driver_7_out,
       driver_8_out, driver_9_out, driver_10_out, driver_11_out, driver_12_out, driver_13_out, driver_14_out,
       driver_15_out, driver_16_out, or_1_out, reg16_1_o0, reg16_1_o1, reg16_1_o2, reg16_1_o3, reg16_1_o4,
       reg16_1_o5, reg16_1_o6, reg16_1_o7, reg16_1_o8, reg16_1_o9, reg16_1_o10, reg16_1_o11, reg16_1_o12,
       reg16_1_o13, reg16_1_o14, reg16_1_o15, undriven, undriven_2, undriven_3;

  assign driver_1_out = W ? D0 : 1'bz;  // Driver driver_1
  assign driver_2_out = W ? D1 : 1'bz;  // Driver driver_2
  assign driver_3_out = W ? D2 : 1'bz;  // Driver driver_3
  assign driver_4_out = W ? D3 : 1'bz;  // Driver driver_4
  assign driver_5_out = W ? D4 : 1'bz;  // Driver driver_5
  assign driver_6_out = W ? D5 : 1'bz;  // Driver driver_6
  assign driver_7_out = W ? D6 : 1'bz;  // Driver driver_7
  assign driver_8_out = W ? D7 : 1'bz;  // Driver driver_8
  assign driver_9_out = undriven ? D8 : 1'bz;  // Driver driver_9
  assign driver_10_out = undriven ? D9 : 1'bz;  // Driver driver_10
  assign driver_11_out = undriven ? D10 : 1'bz;  // Driver driver_11
  assign driver_12_out = undriven ? D11 : 1'bz;  // Driver driver_12
  assign driver_13_out = undriven ? D12 : 1'bz;  // Driver driver_13
  assign driver_14_out = undriven ? D13 : 1'bz;  // Driver driver_14
  assign driver_15_out = undriven ? D14 : 1'bz;  // Driver driver_15
  assign driver_16_out = undriven ? D15 : 1'bz;  // Driver driver_16
  or or_1 (or_1_out, E, W);
  Reg16 reg16_1 (
    .CLK(CLK), .E(1'b1), .R(1'b1), .W(or_1_out), .D0(driver_1_out), .D1(driver_2_out), .D2(driver_3_out),
    .D3(driver_4_out), .D4(driver_5_out), .D5(driver_6_out), .D6(driver_7_out), .D7(driver_8_out),
    .D8(driver_9_out), .D9(driver_10_out), .D10(driver_11_out), .D11(driver_12_out), .D12(driver_13_out),
    .D13(driver_14_out), .D14(driver_15_out), .D15(driver_16_out), .O0(reg16_1_o0), .O1(reg16_1_o1),
    .O2(reg16_1_o2), .O3(reg16_1_o3), .O4(reg16_1_o4), .O5(reg16_1_o5), .O6(reg16_1_o6), .O7(reg16_1_o7),
    .O8(reg16_1_o8), .O9(reg16_1_o9), .O10(reg16_1_o10), .O11(reg16_1_o11), .O12(reg16_1_o12),
    .O13(reg16_1_o13), .O14(reg16_1_o14), .O15(reg16_1_o15));
  Incrementer incrementer_1 (
    .E(E), .D0(reg16_1_o0), .D1(reg16_1_o1), .D2(reg16_1_o2), .D3(reg16_1_o3), .D4(reg16_1_o4),
    .D5(reg16_1_o5), .D6(reg16_1_o6), .D7(reg16_1_o7), .O0(driver_1_out), .O1(driver_2_out),
    .O2(driver_3_out), .O3(driver_4_out), .O4(driver_5_out), .O5(driver_6_out), .O6(driver_7_out),
    .O7(driver_8_out));
  Incrementer incrementer_2 (
    .E(E), .D0(reg16_1_o8), .D1(reg16_1_o9), .D2(reg16_1_o10), .D3(reg16_1_o11), .D4(reg16_1_o12),
    .D5(reg16_1_o13), .D6(reg16_1_o14), .D7(reg16_1_o15), .O0(driver_9_out), .O1(driver_10_out),
    .O2(driver_11_out), .O3(driver_12_out), .O4(driver_13_out), .O5(driver_14_out), .O6(driver_15_out),
    .O7(driver_16_out));
  assign O0 = undriven_2 ? reg16_1_o0 : 1'bz;  // Driver driver_17
  assign O1 = undriven_2 ? reg16_1_o1 : 1'bz;  // Driver driver_18
  assign O2 = undriven_2 ? reg16_1_o2 : 1'bz;  // Driver driver_19
  assign O3 = undriven_2 ? reg16_1_o3 : 1'bz;  // Driver driver_20
  assign O4 = undriven_2 ? reg16_1_o4 : 1'bz;  // Driver driver_21
  assign O5 = undriven_2 ? reg16_1_o5 : 1'bz;  // Driver driver_22
  assign O6 = undriven_2 ? reg16_1_o6 : 1'bz;  // Driver driver_23
  assign O7 = undriven_2 ? reg16_1_o7 : 1'bz;  // Driver driver_24
  assign O8 = undriven_3 ? reg16_1_o8 : 1'bz;  // Driver driver_25
  assign O9 = undriven_3 ? reg16_1_o9 : 1'bz;  // Driver driver_26
  assign O10 = undriven_3 ? reg16_1_o10 : 1'bz;  // Driver driver_27
  assign O11 = undriven_3 ? reg16_1_o11 : 1'bz;  // Driver driver_28
  assign O12 = undriven_3 ? reg16_1_o12 : 1'bz;  // Driver driver_29
  assign O13 = undriven_3 ? reg16_1_o13 : 1'bz;  // Driver driver_30
  assign O14 = undriven_3 ? reg16_1_o14 : 1'bz;  // Driver driver_31
  assign O15 = undriven_3 ? reg16_1_o15 : 1'bz;  // Driver driver_32
endmodule
