// Digital circuit Rising Edge Detector.dig as structural Verilog
module Rising_Edge_Detector (
  input  CLK,
  output OUT
);

  wire not_1_out, not_2_out, not_3_out;

  not not_1 (not_1_out, not_2_out);
  not not_2 (not_2_out, CLK);
  not not_3 (not_3_out, not_1_out);
  and and_1 (OUT, CLK, not_3_out);
endmodule
